// Logisim project Pipline_CPU.circ as structural Verilog: 19 circuits, main circuit main
module main (
);

  wire alu_1_equal, ALU_SRC, and_1_out, and_2_out, and_5_out, Beq, Bne, CLK, comparator_1_gt,
       comparator_2_eq, comparator_3_eq, EX_Beq, EX_Bne, EX_Branch, EX_JAL, EX_JMP, EX_JR, EX_LW,
       ex_mem_1_out_17, ex_mem_1_out_18, ex_mem_1_out_24, EX_RegDst, EX_RegWrite, EX_shiftVar,
       id_ex_1_out_30, id_ex_1_out_31, id_ex_1_out_35, id_ex_1_out_41, id_ex_1_out_42, id_ex_1_out_44, ID_LW,
       JAL, JMP, JR, Load_Used_Detected, MEM_JAL, MEM_RegDst, MEM_RegWrite, mem_wb_1_out_17, mem_wb_1_out_18,
       Mem_Write, MemToReg, not_1_out, not_2_out, not_3_out, not_4_out, not_5_out, not_6_out, or_2_out,
       or_3_out, or_4_out, or_5_out, RegDst, RegWrite, shiftVar, SignedExt, SysCall, WB_DisplayHex, WB_Halt,
       WB_JAL, WB_RegDst, WB_RegWrite, \源寄存器使用情况_1_r1_used , \源寄存器使用情况_1_r2_used ;
  wire [1:0] ALU_Src1, id_ex_1_alu_src1, id_ex_1_r2exmem_2, priority_encoder_3_out, priority_encoder_4_out,
       R2EXMEM, WB_W_num;
  wire [2:0] Branch;
  wire [3:0] ALU_OP, id_ex_1_out_43;
  wire [4:0] EX_Rd, EX_Rt, id_ex_1_shamt_2, if_id_1_rd, if_id_1_rs, if_id_1_rt, if_id_1_rt_2, if_id_1_shamt,
       MEM_Rd, MEM_Rt, multiplexer_2_out, multiplexer_6_out, multiplexer_7_out, multiplexer_11_out, R1_num,
       R2_num, WB_Rd, WB_Rt;
  wire [5:0] EX_Funct, EX_OP;
  wire [15:0] counter_2_q, counter_3_q, counter_4_q, if_id_1_imm;
  wire [25:0] if_id_1_address;
  wire [27:2] UnConditionalAddress;
  wire [31:0] alu_1_result, BeqBneAddress, counter_1_q, counter_5_q, ex_mem_1_alu_result_2, ex_mem_1_ir_2,
       ex_mem_1_pc_2, ex_mem_1_r1_2, ex_mem_1_r2_2, EX_PC, EX_PC_4, HexDataToDisplay, id_ex_1_imm_2,
       id_ex_1_ir_2, id_ex_1_r2_2, ID_V0, if_id_1_ir, if_id_1_pc_2, IF_PC_4, JRAddress,
       mem_wb_1_alu_result_2, mem_wb_1_r1_2, mem_wb_1_wd_2, multiplexer_1_out, multiplexer_5_out,
       multiplexer_8_out, multiplexer_9_out, multiplexer_10_out, multiplexer_12_out, PC_q, ram_1_data,
       regifile_1_r2, register_1_q, rom_1_data, shifter_1_out, WB_IR, WB_PC, WB_PC_4, \符号扩展_1_out_3 ;

  Clock #(.highDuration(1), .lowDuration(1)) \CPU时钟  (.out(CLK));
  Hex_Digit_Display hex_digit_display_1 (.value(register_1_q[27:24]));  // open: dp
  Hex_Digit_Display hex_digit_display_2 (.value(register_1_q[31:28]));  // open: dp
  Register #(.width(32), .trigger("rising"), .Select("low")) register_1 (
    .D(HexDataToDisplay), .Q(register_1_q), .clk(WB_DisplayHex));  // open: en, clr
  Hex_Digit_Display hex_digit_display_3 (.value(register_1_q[23:20]));  // open: dp
  Hex_Digit_Display hex_digit_display_4 (.value(register_1_q[19:16]));  // open: dp
  // Probe on register_1_q
  Hex_Digit_Display hex_digit_display_5 (.value(register_1_q[15:12]));  // open: dp
  Hex_Digit_Display hex_digit_display_6 (.value(register_1_q[11:8]));  // open: dp
  Priority_Encoder #(.select(2), .disabled("Z")) priority_encoder_1 (
    .in0(1'b1), .in1(WB_RegDst), .in2(WB_JAL), .out(WB_W_num));  // open: in3, gs, en_out, en_in
  // Probe on Branch
  Priority_Encoder #(.select(3), .disabled("Z")) priority_encoder_2 (
    .in0(1'b1), .in1(EX_Beq), .in2(EX_Bne), .in3(EX_JMP), .in4(EX_JAL), .in5(EX_JR), .out(Branch));  // open: in6, in7, gs, en_out, en_in
  or or_1 (EX_Branch, EX_Beq, EX_Bne, EX_JMP, EX_JAL, EX_JR);
  Hex_Digit_Display hex_digit_display_7 (.value(register_1_q[7:4]));  // open: dp
  Hex_Digit_Display hex_digit_display_8 (.value(register_1_q[3:0]));  // open: dp
  Multiplexer #(.select(3), .width(32), .disabled("Z"), .enable("true")) multiplexer_1 (
    .in0(IF_PC_4), .in1(BeqBneAddress), .in2(BeqBneAddress),
    .in3({EX_PC_4[31:28], UnConditionalAddress, 2'b00}), .in4({EX_PC_4[31:28], UnConditionalAddress, 2'b00}),
    .in5(JRAddress), .out(multiplexer_1_out), .sel(Branch));  // open: in6, in7, en
  not not_1 (not_1_out, WB_Halt);
  not not_2 (not_2_out, WB_Halt);
  Comparator #(.width(32), .mode("unsigned")) comparator_1 (
    .a(WB_IR), .b({32{1'b0}}), .gt(comparator_1_gt));  // open: eq, lt
  and and_1 (and_1_out, not_4_out, not_3_out);
  not not_3 (not_3_out, WB_Halt);
  not not_4 (not_4_out, Load_Used_Detected);
  Counter #(.width(32), .max('hffffffff), .ongoal("wrap"), .trigger("rising"), .behavior("old")) counter_1 (
    .count(not_1_out), .Q(counter_1_q), .clk(CLK));  // open: load, D, carry, clr, preset
  Counter #(.width(16), .max('hffff), .ongoal("wrap"), .trigger("rising"), .behavior("old")) counter_2 (
    .count(and_2_out), .Q(counter_2_q), .clk(CLK));  // open: load, D, carry, clr, preset
  and and_2 (and_2_out, not_2_out, comparator_1_gt);
  Register #(.width(32), .trigger("rising"), .Select("low")) PC (
    .D(multiplexer_1_out), .en(and_1_out), .Q(PC_q), .clk(CLK));  // open: clr
  // Probe on counter_1_q
  // Probe on counter_2_q
  Adder #(.width(32)) adder_1 (.a(32'h4), .b(PC_q), .out(IF_PC_4));  // open: cin, cout
  IF_ID if_id_1 (
    .instruction(rom_1_data), .EN(not_5_out), .CLK(CLK), .\Clear_同步清零 (or_2_out), .PC(PC_q), .OP(EX_OP),
    .Func(EX_Funct), .Rs(if_id_1_rs), .Rt(if_id_1_rt), .Rd(if_id_1_rd), .Imm(if_id_1_imm),
    .Shamt(if_id_1_shamt), .Address(if_id_1_address), .PC_2(if_id_1_pc_2), .IR(if_id_1_ir),
    .Rt_2(if_id_1_rt_2));
  ROM #(.addrWidth(10), .dataWidth(32), .Select("high")) rom_1 (.addr(PC_q[11:2]), .data(rom_1_data));
  not not_5 (not_5_out, Load_Used_Detected);
  // Probe on if_id_1_ir
  or or_2 (or_2_out, EX_Branch, WB_Halt);
  \源寄存器使用情况  \u_源寄存器使用情况_1  (
    .OP1(EX_OP[0]), .OP2(EX_OP[1]), .OP3(EX_OP[2]), .OP4(EX_OP[3]), .OP5(EX_OP[4]), .OP6(EX_OP[5]),
    .Funct1(EX_Funct[0]), .Funct2(EX_Funct[1]), .Funct3(EX_Funct[2]), .Funct4(EX_Funct[3]),
    .Funct5(EX_Funct[4]), .Funct6(EX_Funct[5]), .R1_Used(\源寄存器使用情况_1_r1_used ),
    .R2_Used(\源寄存器使用情况_1_r2_used ), .LW(ID_LW));
  Counter #(.width(16), .max('hffff), .ongoal("wrap"), .trigger("rising"), .behavior("old")) counter_3 (
    .count(or_3_out), .Q(counter_3_q), .clk(CLK));  // open: load, D, carry, clr, preset
  or or_3 (or_3_out, EX_JMP, EX_JR, EX_JAL);
  Counter #(.width(16), .max('hffff), .ongoal("wrap"), .trigger("rising"), .behavior("old")) counter_4 (
    .count(or_4_out), .Q(counter_4_q), .clk(CLK));  // open: load, D, carry, clr, preset
  or or_4 (or_4_out, EX_Beq, EX_Bne);
  Multiplexer #(.select(2), .width(5), .disabled("Z"), .enable("true")) multiplexer_2 (
    .in0(WB_Rt), .in1(WB_Rd), .in2({5{1'b1}}), .out(multiplexer_2_out), .sel(WB_W_num));  // open: in3, en
  // Probe on if_id_1_rt_2
  // Probe on if_id_1_rd
  // Probe on counter_3_q
  // Probe on counter_4_q
  Multiplexer #(.select(1), .width(5), .disabled("Z"), .enable("true")) multiplexer_3 (
    .in0(if_id_1_rs), .in1(5'b00010), .out(R1_num), .sel(SysCall));  // open: en
  Multiplexer #(.select(1), .width(5), .disabled("Z"), .enable("true")) multiplexer_4 (
    .in0(if_id_1_rt), .in1(5'b00100), .out(R2_num), .sel(SysCall));  // open: en
  // Probe on if_id_1_imm
  \硬布线控制器  \u_硬布线控制器_1  (
    .Func(EX_Funct), .OP(EX_OP), .ALU_OP(ALU_OP), .MemToReg(MemToReg), .MemWrite(Mem_Write),
    .ALU_SRC(ALU_SRC), .RegWrite(RegWrite), .SysCALL(SysCall), .SignedExt(SignedExt), .RegDst(RegDst),
    .JR(JR), .JMP(JMP), .Beq(Beq), .JAL(JAL), .Bne(Bne), .ShiftVar(shiftVar));
  // Probe on R2_num
  // Probe on multiplexer_2_out
  Multiplexer #(.select(1), .width(32), .disabled("Z"), .enable("true")) multiplexer_5 (
    .in0(multiplexer_12_out), .in1(WB_PC_4), .out(multiplexer_5_out), .sel(WB_JAL));  // open: en
  Priority_Encoder #(.select(2), .disabled("Z")) priority_encoder_3 (
    .in0(1'b1), .in1(EX_RegDst), .in2(EX_JAL), .out(priority_encoder_3_out));  // open: in3, gs, en_out, en_in
  // Probe on multiplexer_5_out
  Multiplexer #(.select(2), .width(5), .disabled("Z"), .enable("true")) multiplexer_6 (
    .in0(EX_Rt), .in1(EX_Rd), .in2({5{1'b1}}), .out(multiplexer_6_out), .sel(priority_encoder_3_out));  // open: in3, en
  Counter #(.width(32), .max('hffffffff), .ongoal("wrap"), .trigger("rising"), .behavior("old")) counter_5 (
    .count(Load_Used_Detected), .Q(counter_5_q), .clk(CLK));  // open: load, D, carry, clr, preset
  Regifile regifile_1 (
    .Din(multiplexer_5_out), .Clk(CLK), .R1(ID_V0), .R2(regifile_1_r2), .WE(WB_RegWrite),
    .W_num(multiplexer_2_out), .R1_num(R1_num), .R2_num(R2_num));
  \数据相关检测  \u_数据相关检测_1  (
    .R1_Used(\源寄存器使用情况_1_r1_used ), .R1_num(R1_num), .R2_num(R2_num), .R2_Used(\源寄存器使用情况_1_r2_used ),
    .EX_WriteReg_num(multiplexer_6_out), .MEM_WriteReg_num(multiplexer_7_out), .EX_RegWrite(EX_RegWrite),
    .MEM_RegWrite(MEM_RegWrite), .ALU_Src1(ALU_Src1), .R2EXMEM(R2EXMEM));
  \load_use检测  \load_used检测  (
    .R1_Used(\源寄存器使用情况_1_r1_used ), .R1_num(R1_num), .R2_Used(\源寄存器使用情况_1_r2_used ), .R2_num(R2_num),
    .load_use_Detected(Load_Used_Detected), .EX_WriteReg_num(multiplexer_6_out), .EX_LW(EX_LW));
  // Probe on counter_5_q
  Regifile regifile_2 ();  // open: Din, Clk, R1, R2, WE, W_num, R1_num, R2_num
  // Probe on ID_V0
  \符号扩展  \u_符号扩展_1  (.in_1(if_id_1_imm), .out_3(\符号扩展_1_out_3 ), .in_2(SignedExt));
  // Probe on ALU_Src1
  // Probe on R2EXMEM
  Multiplexer #(.select(2), .width(5), .disabled("Z"), .enable("true")) multiplexer_7 (
    .in0(MEM_Rt), .in1(MEM_Rd), .in2({5{1'b1}}), .out(multiplexer_7_out), .sel(priority_encoder_4_out));  // open: in3, en
  Priority_Encoder #(.select(2), .disabled("Z")) priority_encoder_4 (
    .in0(1'b1), .in1(MEM_RegDst), .in2(MEM_JAL), .out(priority_encoder_4_out));  // open: in3, gs, en_out, en_in
  ID_EX id_ex_1 (
    .in_2(MemToReg), .in_3(RegDst), .in_4(RegWrite), .in_6(Mem_Write), .in_9(JMP), .in_10(JR), .in_11(JAL),
    .in_12(Bne), .in_13(Beq), .in_1(SysCall), .in_14(ALU_OP), .in_15(ALU_SRC), .R1(ID_V0),
    .R2(regifile_1_r2), .Imm(\符号扩展_1_out_3 ), .Shamt(if_id_1_shamt), .Address(if_id_1_address),
    .PC(if_id_1_pc_2), .IR(if_id_1_ir), .CLK(CLK), .out_31(id_ex_1_out_31), .out_32(EX_RegDst),
    .out_33(EX_RegWrite), .out_35(id_ex_1_out_35), .out_38(EX_JMP), .out_39(EX_JR), .out_40(EX_JAL),
    .out_41(id_ex_1_out_41), .out_42(id_ex_1_out_42), .out_30(id_ex_1_out_30), .out_43(id_ex_1_out_43),
    .out_44(id_ex_1_out_44), .R1_2(JRAddress), .R2_2(id_ex_1_r2_2), .Imm_2(id_ex_1_imm_2),
    .Shamt_2(id_ex_1_shamt_2), .Address_2(UnConditionalAddress), .PC_2(EX_PC), .IR_2(id_ex_1_ir_2),
    .\Clear_同步清零高电平有效 (or_5_out), .in_5(JAL), .out_34(EX_JAL), .Rd(if_id_1_rd), .Rd_2(EX_Rd),
    .Rt(if_id_1_rt_2), .Rt_2(EX_Rt), .AUL_Src1(ALU_Src1), .ALU_Src1(id_ex_1_alu_src1), .R2EXMEM(R2EXMEM),
    .R2EXMEM_2(id_ex_1_r2exmem_2), .in_8(ID_LW), .out_37(EX_LW), .in_7(shiftVar), .out_36(EX_shiftVar));  // open: EN
  or or_5 (or_5_out, Load_Used_Detected, EX_Branch, WB_Halt);
  // Probe on id_ex_1_alu_src1
  // Probe on id_ex_1_ir_2
  Adder #(.width(32)) adder_2 (.a(EX_PC), .b(32'h4), .out(EX_PC_4));  // open: cin, cout
  Multiplexer #(.select(2), .width(32), .disabled("Z"), .enable("true")) multiplexer_8 (
    .in0(JRAddress), .in1(ex_mem_1_alu_result_2), .in2(multiplexer_12_out), .in3(ex_mem_1_alu_result_2),
    .out(multiplexer_8_out), .sel(id_ex_1_alu_src1));  // open: en
  Multiplexer #(.select(2), .width(32), .disabled("Z"), .enable("true")) multiplexer_9 (
    .in0(id_ex_1_r2_2), .in1(ex_mem_1_alu_result_2), .in2(multiplexer_12_out), .in3(ex_mem_1_alu_result_2),
    .out(multiplexer_9_out), .sel(id_ex_1_r2exmem_2));  // open: en
  Shifter #(.width(32), .shift("ll")) shifter_1 (.in(id_ex_1_imm_2), .\dist (5'b00010), .out(shifter_1_out));
  // Probe on multiplexer_8_out
  // Probe on multiplexer_10_out
  Multiplexer #(.select(1), .width(32), .disabled("Z"), .enable("true")) multiplexer_10 (
    .in0(multiplexer_9_out), .in1(id_ex_1_imm_2), .out(multiplexer_10_out), .sel(id_ex_1_out_44));  // open: en
  Adder #(.width(32)) adder_3 (.a(EX_PC_4), .b(shifter_1_out), .out(BeqBneAddress));  // open: cin, cout
  ALU alu_1 (
    .shamt(multiplexer_11_out), .X(multiplexer_8_out), .Y(multiplexer_10_out), .AluOP(id_ex_1_out_43),
    .Equal(alu_1_equal), .Result(alu_1_result));  // open: Result_2
  Multiplexer #(.select(1), .width(5), .disabled("Z"), .enable("false")) multiplexer_11 (
    .in0(id_ex_1_shamt_2), .in1(JRAddress[4:0]), .out(multiplexer_11_out), .sel(EX_shiftVar));
  and and_3 (EX_Bne, id_ex_1_out_41, ~alu_1_equal);  // AND_Gate
  and and_4 (EX_Beq, id_ex_1_out_42, alu_1_equal);
  // Probe on alu_1_result
  EX_MEM ex_mem_1 (
    .in_2(id_ex_1_out_31), .in_3(EX_RegDst), .in_4(EX_RegWrite), .in_8(id_ex_1_out_35),
    .ALU_Result(alu_1_result), .R2(multiplexer_9_out), .PC(EX_PC), .IR(id_ex_1_ir_2),
    .out_18(ex_mem_1_out_18), .out_19(MEM_RegDst), .out_20(MEM_RegWrite), .out_24(ex_mem_1_out_24),
    .ALU_Result_2(ex_mem_1_alu_result_2), .R2_2(ex_mem_1_r2_2), .PC_2(ex_mem_1_pc_2), .IR_2(ex_mem_1_ir_2),
    .CLK(CLK), .Clear(WB_Halt), .in_5(EX_JAL), .out_21(MEM_JAL), .Rd(EX_Rd), .Rd_2(MEM_Rd), .Rt(EX_Rt),
    .Rt_2(MEM_Rt), .in_1(id_ex_1_out_30), .out_17(ex_mem_1_out_17), .R1(multiplexer_8_out),
    .R1_2(ex_mem_1_r1_2));  // open: EN
  // Probe on ex_mem_1_alu_result_2
  // Probe on ex_mem_1_r2_2
  // Probe on ex_mem_1_ir_2
  RAM #(.addrWidth(10), .dataWidth(32), .bus("separate"), .Select("high")) ram_1 (
    .addr(ex_mem_1_alu_result_2[11:2]), .din(ex_mem_1_r2_2), .data(ram_1_data), .str(ex_mem_1_out_24),
    .clk(CLK));  // open: sel, ld, clr
  // Probe on ram_1_data
  MEM_WB mem_wb_1 (
    .in_2(ex_mem_1_out_18), .in_3(MEM_RegDst), .in_4(MEM_RegWrite), .ALU_Result(ex_mem_1_alu_result_2),
    .WD(ram_1_data), .PC(ex_mem_1_pc_2), .IR(ex_mem_1_ir_2), .out_18(mem_wb_1_out_18), .out_19(WB_RegDst),
    .out_20(WB_RegWrite), .ALU_Result_2(mem_wb_1_alu_result_2), .WD_2(mem_wb_1_wd_2), .PC_2(WB_PC),
    .IR_2(WB_IR), .CLK(CLK), .Clear(WB_Halt), .in_5(MEM_JAL), .out_21(WB_JAL), .Rd(MEM_Rd), .Rd_2(WB_Rd),
    .Rt(MEM_Rt), .Rt_2(WB_Rt), .in_1(ex_mem_1_out_17), .out_17(mem_wb_1_out_17), .R1(ex_mem_1_r1_2),
    .R1_2(mem_wb_1_r1_2), .R2(ex_mem_1_r2_2), .R2_2(HexDataToDisplay));  // open: EN
  Comparator #(.width(32), .mode("twosComplement")) comparator_2 (
    .a(32'ha), .b(mem_wb_1_r1_2), .eq(comparator_2_eq));  // open: gt, lt
  Comparator #(.width(32), .mode("twosComplement")) comparator_3 (
    .a(32'h22), .b(mem_wb_1_r1_2), .eq(comparator_3_eq));  // open: gt, lt
  Multiplexer #(.select(1), .width(32), .disabled("Z"), .enable("true")) multiplexer_12 (
    .in0(mem_wb_1_alu_result_2), .in1(mem_wb_1_wd_2), .out(multiplexer_12_out), .sel(mem_wb_1_out_18));  // open: en
  // Probe on WB_IR
  not not_6 (not_6_out, WB_Halt);
  and and_5 (and_5_out, comparator_2_eq, mem_wb_1_out_17);
  and and_6 (WB_DisplayHex, comparator_3_eq, mem_wb_1_out_17);
  // Probe on multiplexer_12_out
  Adder #(.width(32)) adder_4 (.a(32'h4), .b(WB_PC), .out(WB_PC_4));  // open: cin, cout
  Register #(.width(1), .trigger("rising"), .Select("low")) register_2 (
    .D(and_5_out), .en(not_6_out), .Q(WB_Halt), .clk(CLK));  // open: clr
  // Probe on nothing

  // Other names for the same wires on the sheet: UnConditionalAddress[31:28] = EX_PC_4[31:28]

  // Notes on the sheet:
  //   数码管输出
  //   PC+4
  //   指令存储器
  //   contents of rom_1 (hex, n*v repeats v):
  //   20110001 8000c05 20110001 20120002 20130003 8000c09 20110001 20120002 20130003 8000c0d 20110001
  //   20120002 20130003 8000c11 20110001 20120002 20130003 c000cb8 20100001 20110001 118fc0 112020
  //   20020022 c 118882 12200001 8000c15 112020 20020022 c 20110001 118880 112020 20020022 c 12200001
  //   8000c1f 20110001 118fc0 112020 20020022 c 1188c3 112020 20020022 c 118903 112020 20020022 c 118903
  //   112020 20020022 c 118903 112020 20020022 c 118903 112020 20020022 c 118903 112020 20020022 c 118903
  //   112020 20020022 c 118903 112020 20020022 c 20100001 109fc0 139fc3 8021 2012000c 24160003 26100001
  //   3210000f 20080008 20090001 139900 2709825 132020 20020022 c 1094022 1500fff9 22100001 2018000f
  //   2188024 108700 20080008 20090001 139902 2709825 132021 20020022 c 1094022 1500fff9 108702 2c9b022
  //   12c00001 8000c50 4020 1084027 84400 3508ffff 82021 20020022 c 2010ffff 20110000 ae300000 22100001
  //   22310004 ae300000 22100001 22310004 ae300000 22100001 22310004 ae300000 22100001 22310004 ae300000
  //   22100001 22310004 ae300000 22100001 22310004 ae300000 22100001 22310004 ae300000 22100001 22310004
  //   ae300000 22100001 22310004 ae300000 22100001 22310004 ae300000 22100001 22310004 ae300000 22100001
  //   22310004 ae300000 22100001 22310004 ae300000 22100001 22310004 ae300000 22100001 22310004 ae300000
  //   22100001 22310004 22100001 8020 2011003c 8e130000 8e340000 274402a 11000002 ae330000 ae140000
  //   2231fffc 1611fff8 102020 20020022 c 22100004 2011003c 1611fff2 2002000a c 20100000 22100001 102020
  //   20020022 c 22100002 102020 20020022 c 22100003 102020 20020022 c 22100004 102020 20020022 c 22100005
  //   102020 20020022 c 22100006 102020 20020022 c 22100007 102020 20020022 c 22100008 102020 20020022
  //   20020022 c 3e00008
  //   Rd
  //   寄存器使用情况检测
  //   OP
  //   Func
  //   Rs
  //   Rt
  //   Imm
  //   Shamt
  //   Address
  //   PC
  //   IR
  //   R1_Used
  //   R2_Used
  //   JMP
  //   JR
  //   SignedExt
  //   OP
  //   Func
  //   SysCall
  //   Beq
  //   Bne
  //   MemToReg
  //   Mem_Write
  //   ALU_OP
  //   ALU_SRC
  //   RegWrite
  //   JAL
  //   RegDst
  //   数据相关检测信号
  //   数据相关检测信号
  //   R1
  //   R2
  //   Imm
  //   Shamt
  //   Address
  //   PC
  //   PC
  //   Rt
  //   Rd
  //   IR
  //   IR
  //   MEM.ALU_Result
  //   WB.Data
  //   PC
  //   IR
  //   ALU_Result
  //   Rt
  //   PC
  //   IR
  //   ALU_Result
  //   WD
  //   PC
  //   IR
endmodule

module \单周期MIPS  (
);

  wire Beq, Bne, CLK, comparator_1_eq, comparator_2_eq, counter_3_carry, Display_Hex, equal, Go, Halt, JAL,
       JR, Jump, not_1_out, or_1_out, or_2_out, or_3_out, RegDst, RST, SignedExt, Syscall,
       \硬布线控制器_2_alu_src , \硬布线控制器_2_beq , \硬布线控制器_2_bne , \硬布线控制器_2_memtoreg , \硬布线控制器_2_memwrite ,
       \硬布线控制器_2_regwrite , \硬布线控制器_3_beq , \硬布线控制器_3_bne , \硬布线控制器_3_jal , \硬布线控制器_3_jmp , \硬布线控制器_3_jr ,
       \硬布线控制器_3_memtoreg , \硬布线控制器_3_memwrite , \硬布线控制器_3_regdst , \硬布线控制器_3_regwrite ,
       \硬布线控制器_3_signedext , \硬布线控制器_3_syscall ;
  wire [1:0] W_num;
  wire [2:0] Branch;
  wire [3:0] \硬布线控制器_2_alu_op ;
  wire [4:0] multiplexer_2_out, multiplexer_3_out, multiplexer_4_out;
  wire [15:0] \总周期数 , \无条件分支数 , \条件分支成功数 ;
  wire [27:0] alu_1_result;
  wire [31:0] alu_2_result, alu_4_result, alu_5_result, LedData, multiplexer_1_out, multiplexer_5_out,
       multiplexer_6_out, multiplexer_7_out, PC_2_q, PC_q, ram_1_data, regifile_2_r1, rt, shifter_1_out,
       \符号扩展_1_out_3 ;
  wire [31:2] rom_1_data;
  wire [31:26] rom_1_data_2;

  Button \u_总复位  (.out(RST));
  Button u_Go (.out(Go));
  Clock #(.highDuration(1), .lowDuration(1)) clock_1 (.out(CLK));
  Hex_Digit_Display hex_digit_display_1 (.value(LedData[27:24]));  // open: dp
  Hex_Digit_Display hex_digit_display_2 (.value(LedData[31:28]));  // open: dp
  Priority_Encoder #(.select(3), .disabled("Z")) priority_encoder_1 (
    .in0(1'b1), .in1(JR), .in2(Jump), .in3(JAL), .in4(Bne), .in5(Beq), .out(Branch));  // open: in6, in7, gs, en_out, en_in
  Priority_Encoder #(.select(2), .disabled("Z")) priority_encoder_2 (
    .in0(1'b1), .in1(RegDst), .in2(JAL), .out(W_num));  // open: in3, gs, en_out, en_in
  // Probe on multiplexer_1_out
  Multiplexer #(.select(3), .width(32), .disabled("Z"), .enable("true")) multiplexer_1 (
    .in0({rom_1_data[31:28], alu_1_result}), .in1(regifile_2_r1), .in2({rom_1_data, 2'b00}),
    .in3({rom_1_data, 2'b00}), .in4(alu_5_result), .in5(alu_5_result), .out(multiplexer_1_out), .sel(Branch));  // open: in6, in7, en
  // Probe on {rom_1_data, 2'b00}
  Hex_Digit_Display hex_digit_display_3 (.value(LedData[19:16]));  // open: dp
  Hex_Digit_Display hex_digit_display_4 (.value(LedData[23:20]));  // open: dp
  Register #(.width(32), .trigger("rising"), .Select("low")) PC (
    .D(multiplexer_1_out), .en(not_1_out), .Q(PC_q), .clk(CLK), .clr(RST));
  not not_1 (not_1_out, Halt);
  or or_1 (or_1_out, Jump, JR, JAL);
  or or_2 (or_2_out, Beq, Bne);
  Register #(.width(32), .trigger("rising"), .Select("low")) PC_2 (.D(alu_2_result), .Q(PC_2_q));  // open: en, clk, clr
  Hex_Digit_Display hex_digit_display_5 (.value(LedData[15:12]));  // open: dp
  Hex_Digit_Display hex_digit_display_6 (.value(LedData[11:8]));  // open: dp
  // Probe on PC_q[11:2]
  Counter #(.width(16), .max('hffff), .ongoal("wrap"), .trigger("rising"), .behavior("old")) counter_1 (
    .count(or_1_out), .Q(\无条件分支数 ), .clk(CLK), .clr(RST));  // open: load, D, carry, preset
  Counter #(.width(16), .max('hffff), .ongoal("wrap"), .trigger("rising"), .behavior("old")) counter_2 (
    .count(or_2_out), .Q(\条件分支成功数 ), .clk(CLK), .clr(RST));  // open: load, D, carry, preset
  Hex_Digit_Display hex_digit_display_7 (.value(LedData[7:4]));  // open: dp
  Hex_Digit_Display hex_digit_display_8 (.value(LedData[3:0]));  // open: dp
  ALU alu_1 (
    .X(PC_q), .Y(32'h4), .AluOP(4'b0101), .Result({rom_1_data[31:28], alu_1_result}));  // open: shamt, Equal, Result_2
  ALU alu_2 (.X(PC_2_q), .Y(32'h4), .AluOP(4'b0101), .Result(alu_2_result));  // open: shamt, Equal, Result_2
  ROM #(.addrWidth(10), .dataWidth(32), .Select("high")) rom_1 (
    .addr(PC_q[11:2]), .data({rom_1_data_2, rom_1_data[27:2]}));
  or or_3 (or_3_out, Halt, CLK);
  ROM #(.addrWidth(10), .dataWidth(32), .Select("high")) \u_指令存储器  (.addr(PC_2_q[11:2]));  // open: data
  // Probe on \总周期数 
  // Probe on \无条件分支数 
  // Probe on \条件分支成功数 
  Counter #(.width(16), .max('hffff), .ongoal("wrap"), .trigger("rising"), .behavior("old")) counter_3 (
    .Q(\总周期数 ), .carry(counter_3_carry), .clk(or_3_out), .clr(RST));  // open: load, D, count, preset
  \硬布线控制器  \u_硬布线控制器_1  ();  // open: Func, OP, ALU_OP, MemToReg, MemWrite, ALU_SRC, RegWrite, SysCALL, SignedExt, RegDst, JR, JMP, Beq, JAL, Bne, ShiftVar
  \硬布线控制器  \u_硬布线控制器_2  (
    .Func(rom_1_data[7:2]), .OP(rom_1_data_2), .ALU_OP(\硬布线控制器_2_alu_op ), .MemToReg(\硬布线控制器_2_memtoreg ),
    .MemWrite(\硬布线控制器_2_memwrite ), .ALU_SRC(\硬布线控制器_2_alu_src ), .RegWrite(\硬布线控制器_2_regwrite ),
    .SysCALL(Syscall), .SignedExt(SignedExt), .RegDst(RegDst), .JR(JR), .JMP(Jump), .Beq(\硬布线控制器_2_beq ),
    .JAL(JAL), .Bne(\硬布线控制器_2_bne ));  // open: ShiftVar
  Multiplexer #(.select(1), .width(5), .disabled("Z"), .enable("true")) multiplexer_2 (
    .in0(rom_1_data[27:23]), .in1(5'b00010), .out(multiplexer_2_out), .sel(Syscall));  // open: en
  Multiplexer #(.select(1), .width(5), .disabled("Z"), .enable("true")) multiplexer_3 (
    .in0(rom_1_data[22:18]), .in1(5'b00100), .out(multiplexer_3_out), .sel(Syscall));  // open: en
  Multiplexer #(.select(2), .width(5), .disabled("Z"), .enable("true")) multiplexer_4 (
    .in0(rom_1_data[22:18]), .in1(rom_1_data[17:13]), .in2({5{1'b1}}), .out(multiplexer_4_out), .sel(W_num));  // open: in3, en
  Multiplexer #(.select(1), .width(32), .disabled("Z"), .enable("true")) multiplexer_5 (
    .in0(multiplexer_7_out), .in1({rom_1_data[31:28], alu_1_result}), .out(multiplexer_5_out), .sel(JAL));  // open: en
  \符号扩展  \u_符号扩展_1  (.in_1(rom_1_data[17:2]), .out_3(\符号扩展_1_out_3 ), .in_2(SignedExt));
  Regifile regifile_1 ();  // open: Din, Clk, R1, R2, WE, W_num, R1_num, R2_num
  and and_1 (Beq, equal, \硬布线控制器_2_beq );
  and and_2 (Bne, ~equal, \硬布线控制器_2_bne );  // AND_Gate
  Regifile regifile_2 (
    .Din(multiplexer_5_out), .Clk(CLK), .R1(regifile_2_r1), .R2(rt), .WE(\硬布线控制器_2_regwrite ),
    .W_num(multiplexer_4_out), .R1_num(multiplexer_2_out), .R2_num(multiplexer_3_out));
  Comparator #(.width(32), .mode("unsigned")) comparator_1 (
    .a(regifile_2_r1), .b(32'h22), .eq(comparator_1_eq));  // open: gt, lt
  Comparator #(.width(32), .mode("unsigned")) comparator_2 (
    .a(regifile_2_r1), .b(32'ha), .eq(comparator_2_eq));  // open: gt, lt
  Register #(.width(32), .trigger("rising"), .Select("low")) register_1 (
    .D(rt), .Q(LedData), .clk(Display_Hex), .clr(RST));  // open: en
  ALU alu_3 ();  // open: shamt, X, Y, AluOP, Equal, Result, Result_2
  and and_3 (Display_Hex, comparator_1_eq, Syscall);
  and and_4 (Halt, Syscall, comparator_2_eq);
  Multiplexer #(.select(1), .width(32), .disabled("Z"), .enable("true")) multiplexer_6 (
    .in0(rt), .in1(\符号扩展_1_out_3 ), .out(multiplexer_6_out), .sel(\硬布线控制器_2_alu_src ));  // open: en
  Shifter #(.width(32), .shift("ll")) shifter_1 (.in(\符号扩展_1_out_3 ), .\dist (5'b00010), .out(shifter_1_out));
  ALU alu_4 (
    .shamt(rom_1_data[12:8]), .X(regifile_2_r1), .Y(multiplexer_6_out), .AluOP(\硬布线控制器_2_alu_op ),
    .Equal(equal), .Result(alu_4_result));  // open: Result_2
  ALU alu_5 (
    .X(shifter_1_out), .Y({rom_1_data[31:28], alu_1_result}), .AluOP(4'b0101), .Result(alu_5_result));  // open: shamt, Equal, Result_2
  RAM #(.addrWidth(10), .dataWidth(32), .bus("separate"), .Select("high")) \u_数据存储器  ();  // open: addr, din, data, str, sel, clk, ld, clr
  RAM #(.addrWidth(10), .dataWidth(32), .bus("separate"), .Select("high")) ram_1 (
    .addr(alu_4_result[11:2]), .din(rt), .data(ram_1_data), .str(\硬布线控制器_2_memwrite ), .clk(CLK), .clr(RST));  // open: sel, ld
  Multiplexer #(.select(1), .width(32), .disabled("Z"), .enable("true")) multiplexer_7 (
    .in0(alu_4_result), .in1(ram_1_data), .out(multiplexer_7_out), .sel(\硬布线控制器_2_memtoreg ));  // open: en
  \硬布线控制器  \u_硬布线控制器_3  (
    .MemToReg(\硬布线控制器_3_memtoreg ), .MemWrite(\硬布线控制器_3_memwrite ), .RegWrite(\硬布线控制器_3_regwrite ),
    .SysCALL(\硬布线控制器_3_syscall ), .SignedExt(\硬布线控制器_3_signedext ), .RegDst(\硬布线控制器_3_regdst ),
    .JR(\硬布线控制器_3_jr ), .JMP(\硬布线控制器_3_jmp ), .Beq(\硬布线控制器_3_beq ), .JAL(\硬布线控制器_3_jal ), .Bne(\硬布线控制器_3_bne ));  // open: Func, OP, ALU_OP, ALU_SRC, ShiftVar
  // Probe on nothing

  // Notes on the sheet:
  //   JR无条件跳转到(RS)的地址
  //   计算PC+4逻辑
  //   计算PC+4逻辑
  //   数码管输出
  //   指令存储器
  //   OP
  //   rs
  //   指令字
  //   contents of rom_1 (hex, n*v repeats v):
  //   20110001 8000c05 20110001 20120002 20130003 8000c09 20110001 20120002 20130003 8000c0d 20110001
  //   20120002 20130003 8000c11 20110001 20120002 20130003 c000cb8 20100001 20110001 118fc0 112020
  //   20020022 c 118882 12200001 8000c15 112020 20020022 c 20110001 118880 112020 20020022 c 12200001
  //   8000c1f 20110001 118fc0 112020 20020022 c 1188c3 112020 20020022 c 118903 112020 20020022 c 118903
  //   112020 20020022 c 118903 112020 20020022 c 118903 112020 20020022 c 118903 112020 20020022 c 118903
  //   112020 20020022 c 118903 112020 20020022 c 20100001 109fc0 139fc3 8021 2012000c 24160003 26100001
  //   3210000f 20080008 20090001 139900 2709825 132020 20020022 c 1094022 1500fff9 22100001 2018000f
  //   2188024 108700 20080008 20090001 139902 2709825 132021 20020022 c 1094022 1500fff9 108702 2c9b022
  //   12c00001 8000c50 4020 1084027 84400 3508ffff 82021 20020022 c 2010ffff 20110000 ae300000 22100001
  //   22310004 ae300000 22100001 22310004 ae300000 22100001 22310004 ae300000 22100001 22310004 ae300000
  //   22100001 22310004 ae300000 22100001 22310004 ae300000 22100001 22310004 ae300000 22100001 22310004
  //   ae300000 22100001 22310004 ae300000 22100001 22310004 ae300000 22100001 22310004 ae300000 22100001
  //   22310004 ae300000 22100001 22310004 ae300000 22100001 22310004 ae300000 22100001 22310004 ae300000
  //   22100001 22310004 22100001 8020 2011003c 8e130000 8e340000 274402a 11000002 ae330000 ae140000
  //   2231fffc 1611fff8 102020 20020022 c 22100004 2011003c 1611fff2 2002000a c 20100000 22100001 102020
  //   20020022 c 22100002 102020 20020022 c 22100003 102020 20020022 c 22100004 102020 20020022 c 22100005
  //   102020 20020022 c 22100006 102020 20020022 c 22100007 102020 20020022 c 22100008 102020 20020022
  //   20020022 c 3e00008
  //   rt
  //   rd
  //   shamt
  //   address
  //   J型指令地址的生成
  //   contents of 指令存储器 (hex, n*v repeats v):
  //   20110001 8000c05 20110001 20120002 20130003 8000c09 20110001 20120002 20130003 8000c0d 20110001
  //   20120002 20130003 8000c11 20110001 20120002 20130003 c000cb8 20100001 20110001 118fc0 112020
  //   20020022 c 118882 12200001 8000c15 112020 20020022 c 20110001 118880 112020 20020022 c 12200001
  //   8000c1f 20110001 118fc0 112020 20020022 c 1188c3 112020 20020022 c 118903 112020 20020022 c 118903
  //   112020 20020022 c 118903 112020 20020022 c 118903 112020 20020022 c 118903 112020 20020022 c 118903
  //   112020 20020022 c 118903 112020 20020022 c 20100001 109fc0 139fc3 8021 2012000c 24160003 26100001
  //   3210000f 20080008 20090001 139900 2709825 132020 20020022 c 1094022 1500fff9 22100001 2018000f
  //   2188024 108700 20080008 20090001 139902 2709825 132021 20020022 c 1094022 1500fff9 108702 2c9b022
  //   12c00001 8000c50 4020 1084027 84400 3508ffff 82021 20020022 c 2010ffff 20110000 ae300000 22100001
  //   22310004 ae300000 22100001 22310004 ae300000 22100001 22310004 ae300000 22100001 22310004 ae300000
  //   22100001 22310004 ae300000 22100001 22310004 ae300000 22100001 22310004 ae300000 22100001 22310004
  //   ae300000 22100001 22310004 ae300000 22100001 22310004 ae300000 22100001 22310004 ae300000 22100001
  //   22310004 ae300000 22100001 22310004 ae300000 22100001 22310004 ae300000 22100001 22310004 ae300000
  //   22100001 22310004 22100001 8020 2011003c 8e130000 8e340000 274402a 11000002 ae330000 ae140000
  //   2231fffc 1611fff8 102020 20020022 c 22100004 2011003c 1611fff2 2002000a c 20100000 22100001 102020
  //   20020022 c 22100002 102020 20020022 c 22100003 102020 20020022 c 22100004 102020 20020022 c 22100005
  //   102020 20020022 c 22100006 102020 20020022 c 22100007 102020 20020022 c 22100008 102020 20020022
  //   20020022 c 3e00008
  //   JMP
  //   JR
  //   OP
  //   Func
  //   Func
  //   立即数
  //   Beq
  //   Bne
  //   MemToReg
  //   MemWrite
  //   AluOP
  //   AluSrcB
  //   RegWrite
  //   JAL
  //   RegDst
  //   Syscall
  //   总复位信号应将除ROM以外所有存储组件全部清零
  //   数码管输出应该用寄存器锁存，否则显示数据只能一闪而过
  //   可以通过项目增加Logisim库的方式将前几次实验完成的电路作为子电路引入到本电路中使用
  //   计算跳转地址
  //   sw指令rt通过这条数据通路传送到RAM
  //   选择将ALU计算结果或者内存读出的结果送到寄存器堆的数据输入端
  //   JMP
  //   JR
  //   SignedExt
  //   OP
  //   Func
  //   SysCall
  //   Beq
  //   Bne
  //   MemToReg
  //   Mem_Write
  //   ALU_OP
  //   ALU_SRC
  //   RegWrite
  //   JAL
  //   RegDst
endmodule

// 单周期硬布线控制器
module \硬布线控制器  (
  input  [5:0] OP,
  input  [5:0] Func,
  output [3:0] ALU_OP,
  output MemToReg,
  output MemWrite,
  output ALU_SRC,
  output RegWrite,
  output SysCALL,
  output SignedExt,
  output RegDst,
  output Beq,
  output Bne,
  output JR,
  output JMP,
  output JAL,
  output ShiftVar
);

  \运算控制器  \u_运算控制器_1  (
    .OP0(OP[0]), .OP1(OP[1]), .OP2(OP[2]), .OP3(OP[3]), .OP4(OP[4]), .OP5(OP[5]), .F0(Func[0]), .F1(Func[1]),
    .F2(Func[2]), .F3(Func[3]), .F4(Func[4]), .F5(Func[5]), .S0(ALU_OP[0]), .S1(ALU_OP[1]), .S2(ALU_OP[2]),
    .S3(ALU_OP[3]));
  \控制信号生成  \u_控制信号生成_1  (
    .OP0(OP[0]), .OP1(OP[1]), .OP2(OP[2]), .OP3(OP[3]), .OP4(OP[4]), .OP5(OP[5]), .F0(Func[0]), .F1(Func[1]),
    .F2(Func[2]), .F3(Func[3]), .F4(Func[4]), .F5(Func[5]), .MemToReg(MemToReg), .MemWrite(MemWrite),
    .ALU_SRC(ALU_SRC), .RegWrite(RegWrite), .SysCALL(SysCALL), .SignedExt(SignedExt), .RegDst(RegDst),
    .BEQ(Beq), .BNE(Bne), .JR(JR), .JMP(JMP), .JAL(JAL));
  \控制信号生成2  \u_控制信号生成2_1  (
    .OP0(OP[0]), .OP1(OP[1]), .OP2(OP[2]), .OP3(OP[3]), .OP4(OP[4]), .OP5(OP[5]), .F0(Func[0]), .F1(Func[1]),
    .F2(Func[2]), .F3(Func[3]), .F4(Func[4]), .F5(Func[5]), .ShiftVar(ShiftVar));

  // Other names for the same wires on the sheet: OP_CODE[5:0] = OP

  // Notes on the sheet:
  //   运算器控制器，根据指令生成运算器功能选择信号
  //   控制信号生成，产生数据通路需要的其他控制信号
endmodule

// 运算器控制器
module \运算控制器  (
  input  OP0,
  input  OP1,
  input  OP2,
  input  OP3,
  input  OP4,
  input  OP5,
  input  F0,
  input  F1,
  input  F2,
  input  F3,
  input  F4,
  input  F5,
  output S0,
  output S1,
  output S2,
  output S3
);

  wire and_1_out, and_2_out, and_3_out, and_4_out, and_5_out, and_6_out, and_7_out, and_8_out, and_9_out,
       and_10_out, and_11_out, and_12_out, and_13_out, and_14_out, and_15_out, and_16_out, and_17_out,
       and_18_out, and_19_out, and_20_out, and_21_out, and_22_out, and_23_out, and_24_out, and_25_out,
       and_26_out, and_27_out, and_28_out, and_29_out, and_30_out, and_31_out, and_32_out, and_33_out,
       and_34_out, and_35_out, and_36_out, and_37_out, and_38_out, and_39_out, and_40_out, and_41_out,
       and_42_out, and_43_out, and_44_out, not_1_out, not_2_out, not_3_out, not_4_out, not_5_out, not_6_out,
       not_7_out, not_8_out, not_9_out, not_10_out, not_11_out, not_12_out, not_13_out, not_14_out,
       not_15_out, not_16_out, not_17_out, not_18_out, not_19_out, not_20_out, not_21_out, not_22_out,
       not_23_out, not_24_out, not_25_out, not_26_out, not_27_out, not_28_out, not_29_out, not_30_out,
       not_31_out, not_32_out, not_33_out, not_34_out, not_35_out, not_36_out, not_37_out, not_38_out,
       not_39_out, not_40_out, not_41_out, not_42_out, not_43_out, not_44_out, not_45_out, not_46_out,
       not_47_out, not_48_out, not_49_out, not_50_out, not_51_out, not_52_out, not_53_out, not_54_out,
       not_55_out, not_56_out, not_57_out, not_58_out, not_59_out, not_60_out, not_61_out, not_62_out,
       not_63_out, not_64_out, not_65_out, not_66_out, not_67_out, not_68_out, not_69_out, not_70_out,
       not_71_out, not_72_out, not_73_out, not_74_out, not_75_out, not_76_out, not_77_out, not_78_out,
       not_79_out, not_80_out, not_81_out, not_82_out, not_83_out, not_84_out, not_85_out, not_86_out,
       not_87_out, not_88_out, not_89_out, not_90_out, not_91_out, not_92_out, not_93_out, not_94_out,
       not_95_out, not_96_out, not_97_out, not_98_out, not_99_out, not_100_out, not_101_out, not_102_out,
       not_103_out, not_104_out, not_105_out, not_106_out, not_107_out, not_108_out, not_109_out,
       not_110_out, not_111_out, not_112_out, not_113_out, not_114_out, not_115_out, not_116_out,
       not_117_out, not_118_out, not_119_out, not_120_out, not_121_out, not_122_out, not_123_out,
       not_124_out, not_125_out, not_126_out, not_127_out, not_128_out, not_129_out, not_130_out,
       not_131_out, not_132_out, not_133_out, not_134_out, not_135_out, not_136_out, not_137_out,
       not_138_out, not_139_out, not_140_out, not_141_out, not_142_out, not_143_out, not_144_out,
       not_145_out, not_146_out, not_147_out, not_148_out, not_149_out, not_150_out, not_151_out,
       not_152_out, not_153_out, not_154_out, not_155_out, not_156_out, not_157_out, not_158_out,
       not_159_out, not_160_out, not_161_out, not_162_out, not_163_out, not_164_out, not_165_out,
       not_166_out, not_167_out, not_168_out, not_169_out, not_170_out, not_171_out, not_172_out,
       not_173_out, not_174_out, not_175_out, not_176_out, not_177_out, not_178_out, not_179_out,
       not_180_out, not_181_out, not_182_out, not_183_out, not_184_out, not_185_out, not_186_out,
       not_187_out, not_188_out, not_189_out, not_190_out, not_191_out, not_192_out, not_193_out,
       not_194_out, not_195_out, not_196_out, not_197_out, not_198_out, not_199_out, not_200_out,
       not_201_out, not_202_out, not_203_out, not_204_out, not_205_out, not_206_out, not_207_out,
       not_208_out, not_209_out, not_210_out, not_211_out, not_212_out, not_213_out, not_214_out,
       not_215_out, not_216_out, not_217_out, not_218_out, not_219_out, not_220_out, not_221_out,
       not_222_out, not_223_out, not_224_out, not_225_out, not_226_out, not_227_out, not_228_out,
       not_229_out, not_230_out, not_231_out, not_232_out, not_233_out, not_234_out, not_235_out,
       not_236_out, not_237_out, not_238_out, not_239_out, not_240_out, not_241_out, not_242_out,
       not_243_out, not_244_out, not_245_out, not_246_out, not_247_out, not_248_out, not_249_out,
       not_250_out, not_251_out, not_252_out, not_253_out, not_254_out, not_255_out, not_256_out,
       not_257_out, not_258_out, not_259_out, not_260_out, not_261_out, not_262_out, not_263_out,
       not_264_out, not_265_out, not_266_out, not_267_out, not_268_out, not_269_out, not_270_out,
       not_271_out, not_272_out, not_273_out, not_274_out, not_275_out, not_276_out, not_277_out,
       not_278_out, not_279_out, not_280_out, not_281_out, not_282_out, not_283_out, not_284_out,
       not_285_out, not_286_out, not_287_out, not_288_out, not_289_out, not_290_out, not_291_out,
       not_292_out, not_293_out, not_294_out, not_295_out, not_296_out, not_297_out, not_298_out,
       not_299_out, not_300_out, not_301_out, not_302_out, not_303_out;

  not not_1 (not_1_out, OP5);
  not not_2 (not_2_out, OP4);
  not not_3 (not_3_out, OP3);
  not not_4 (not_4_out, OP2);
  not not_5 (not_5_out, OP1);
  not not_6 (not_6_out, OP0);
  not not_7 (not_7_out, F5);
  not not_8 (not_8_out, F4);
  not not_9 (not_9_out, F3);
  not not_10 (not_10_out, F2);
  not not_11 (not_11_out, OP5);
  not not_12 (not_12_out, OP4);
  not not_13 (not_13_out, OP3);
  not not_14 (not_14_out, OP2);
  not not_15 (not_15_out, OP1);
  not not_16 (not_16_out, OP0);
  not not_17 (not_17_out, F4);
  not not_18 (not_18_out, F3);
  not not_19 (not_19_out, F2);
  not not_20 (not_20_out, F1);
  not not_21 (not_21_out, F0);
  not not_22 (not_22_out, OP5);
  not not_23 (not_23_out, OP4);
  not not_24 (not_24_out, OP3);
  not not_25 (not_25_out, OP2);
  not not_26 (not_26_out, OP1);
  not not_27 (not_27_out, OP0);
  not not_28 (not_28_out, F4);
  not not_29 (not_29_out, F3);
  not not_30 (not_30_out, F2);
  not not_31 (not_31_out, F1);
  not not_32 (not_32_out, OP5);
  not not_33 (not_33_out, OP4);
  not not_34 (not_34_out, OP3);
  not not_35 (not_35_out, OP2);
  not not_36 (not_36_out, OP1);
  not not_37 (not_37_out, OP0);
  not not_38 (not_38_out, F4);
  not not_39 (not_39_out, F3);
  not not_40 (not_40_out, F1);
  not not_41 (not_41_out, F0);
  not not_42 (not_42_out, OP5);
  not not_43 (not_43_out, OP4);
  not not_44 (not_44_out, OP3);
  not not_45 (not_45_out, OP2);
  not not_46 (not_46_out, OP1);
  not not_47 (not_47_out, OP0);
  not not_48 (not_48_out, F4);
  not not_49 (not_49_out, F2);
  not not_50 (not_50_out, F0);
  not not_51 (not_51_out, OP5);
  not not_52 (not_52_out, OP4);
  not not_53 (not_53_out, OP2);
  not not_54 (not_54_out, OP1);
  not not_55 (not_55_out, OP0);
  not not_56 (not_56_out, OP5);
  not not_57 (not_57_out, OP4);
  not not_58 (not_58_out, OP1);
  not not_59 (not_59_out, OP0);
  not not_60 (not_60_out, OP5);
  not not_61 (not_61_out, OP4);
  not not_62 (not_62_out, OP2);
  not not_63 (not_63_out, OP1);
  not not_64 (not_64_out, OP5);
  not not_65 (not_65_out, OP4);
  not not_66 (not_66_out, OP2);
  not not_67 (not_67_out, OP0);
  not not_68 (not_68_out, OP4);
  not not_69 (not_69_out, OP3);
  not not_70 (not_70_out, OP2);
  not not_71 (not_71_out, OP4);
  not not_72 (not_72_out, OP2);
  not not_73 (not_73_out, OP5);
  not not_74 (not_74_out, OP4);
  not not_75 (not_75_out, OP3);
  not not_76 (not_76_out, OP2);
  not not_77 (not_77_out, OP1);
  not not_78 (not_78_out, OP0);
  not not_79 (not_79_out, F4);
  not not_80 (not_80_out, F3);
  not not_81 (not_81_out, F0);
  not not_82 (not_82_out, OP5);
  not not_83 (not_83_out, OP4);
  not not_84 (not_84_out, OP3);
  not not_85 (not_85_out, OP2);
  not not_86 (not_86_out, OP1);
  not not_87 (not_87_out, OP0);
  not not_88 (not_88_out, F5);
  not not_89 (not_89_out, F4);
  not not_90 (not_90_out, F3);
  not not_91 (not_91_out, OP5);
  not not_92 (not_92_out, OP4);
  not not_93 (not_93_out, OP0);
  not not_94 (not_94_out, OP5);
  not not_95 (not_95_out, OP4);
  not not_96 (not_96_out, OP3);
  not not_97 (not_97_out, OP2);
  not not_98 (not_98_out, OP1);
  not not_99 (not_99_out, OP0);
  not not_100 (not_100_out, F5);
  not not_101 (not_101_out, F4);
  not not_102 (not_102_out, F3);
  not not_103 (not_103_out, F2);
  not not_104 (not_104_out, F0);
  not not_105 (not_105_out, OP5);
  not not_106 (not_106_out, OP4);
  not not_107 (not_107_out, OP3);
  not not_108 (not_108_out, OP2);
  not not_109 (not_109_out, OP1);
  not not_110 (not_110_out, OP0);
  not not_111 (not_111_out, F4);
  not not_112 (not_112_out, F3);
  not not_113 (not_113_out, F2);
  not not_114 (not_114_out, F0);
  not not_115 (not_115_out, OP5);
  not not_116 (not_116_out, OP4);
  not not_117 (not_117_out, OP3);
  not not_118 (not_118_out, OP2);
  not not_119 (not_119_out, OP1);
  not not_120 (not_120_out, OP0);
  not not_121 (not_121_out, F4);
  not not_122 (not_122_out, F3);
  not not_123 (not_123_out, F1);
  not not_124 (not_124_out, F0);
  not not_125 (not_125_out, OP5);
  not not_126 (not_126_out, OP4);
  not not_127 (not_127_out, OP3);
  not not_128 (not_128_out, OP2);
  not not_129 (not_129_out, OP1);
  not not_130 (not_130_out, OP0);
  not not_131 (not_131_out, F4);
  not not_132 (not_132_out, F3);
  not not_133 (not_133_out, OP5);
  not not_134 (not_134_out, OP4);
  not not_135 (not_135_out, OP3);
  not not_136 (not_136_out, OP2);
  not not_137 (not_137_out, OP1);
  not not_138 (not_138_out, OP0);
  not not_139 (not_139_out, F4);
  not not_140 (not_140_out, F2);
  not not_141 (not_141_out, F0);
  not not_142 (not_142_out, OP5);
  not not_143 (not_143_out, OP4);
  not not_144 (not_144_out, OP1);
  not not_145 (not_145_out, OP0);
  not not_146 (not_146_out, OP5);
  not not_147 (not_147_out, OP4);
  not not_148 (not_148_out, OP2);
  not not_149 (not_149_out, OP0);
  not not_150 (not_150_out, OP5);
  not not_151 (not_151_out, OP4);
  not not_152 (not_152_out, OP3);
  not not_153 (not_153_out, OP2);
  not not_154 (not_154_out, OP1);
  not not_155 (not_155_out, OP0);
  not not_156 (not_156_out, F4);
  not not_157 (not_157_out, F3);
  not not_158 (not_158_out, F2);
  not not_159 (not_159_out, OP5);
  not not_160 (not_160_out, OP4);
  not not_161 (not_161_out, OP3);
  not not_162 (not_162_out, OP2);
  not not_163 (not_163_out, OP1);
  not not_164 (not_164_out, OP0);
  not not_165 (not_165_out, F5);
  not not_166 (not_166_out, F4);
  not not_167 (not_167_out, F3);
  not not_168 (not_168_out, F0);
  not not_169 (not_169_out, OP5);
  not not_170 (not_170_out, OP4);
  not not_171 (not_171_out, OP3);
  not not_172 (not_172_out, OP2);
  not not_173 (not_173_out, OP1);
  not not_174 (not_174_out, OP0);
  not not_175 (not_175_out, F4);
  not not_176 (not_176_out, F3);
  not not_177 (not_177_out, F2);
  not not_178 (not_178_out, F1);
  not not_179 (not_179_out, F0);
  not not_180 (not_180_out, OP5);
  not not_181 (not_181_out, OP4);
  not not_182 (not_182_out, OP3);
  not not_183 (not_183_out, OP2);
  not not_184 (not_184_out, OP1);
  not not_185 (not_185_out, OP0);
  not not_186 (not_186_out, F4);
  not not_187 (not_187_out, F3);
  not not_188 (not_188_out, F2);
  not not_189 (not_189_out, F1);
  not not_190 (not_190_out, OP5);
  not not_191 (not_191_out, OP4);
  not not_192 (not_192_out, OP3);
  not not_193 (not_193_out, OP2);
  not not_194 (not_194_out, OP1);
  not not_195 (not_195_out, OP0);
  not not_196 (not_196_out, F4);
  not not_197 (not_197_out, F3);
  not not_198 (not_198_out, F2);
  not not_199 (not_199_out, F0);
  not not_200 (not_200_out, OP5);
  not not_201 (not_201_out, OP4);
  not not_202 (not_202_out, OP3);
  not not_203 (not_203_out, OP2);
  not not_204 (not_204_out, OP1);
  not not_205 (not_205_out, OP0);
  not not_206 (not_206_out, F4);
  not not_207 (not_207_out, F3);
  not not_208 (not_208_out, F1);
  not not_209 (not_209_out, F0);
  not not_210 (not_210_out, OP5);
  not not_211 (not_211_out, OP4);
  not not_212 (not_212_out, OP3);
  not not_213 (not_213_out, OP2);
  not not_214 (not_214_out, OP1);
  not not_215 (not_215_out, OP0);
  not not_216 (not_216_out, F4);
  not not_217 (not_217_out, F2);
  not not_218 (not_218_out, OP5);
  not not_219 (not_219_out, OP4);
  not not_220 (not_220_out, OP2);
  not not_221 (not_221_out, OP1);
  not not_222 (not_222_out, OP0);
  not not_223 (not_223_out, OP5);
  not not_224 (not_224_out, OP4);
  not not_225 (not_225_out, OP1);
  not not_226 (not_226_out, OP0);
  not not_227 (not_227_out, OP5);
  not not_228 (not_228_out, OP4);
  not not_229 (not_229_out, OP2);
  not not_230 (not_230_out, OP1);
  not not_231 (not_231_out, OP4);
  not not_232 (not_232_out, OP3);
  not not_233 (not_233_out, OP2);
  not not_234 (not_234_out, OP4);
  not not_235 (not_235_out, OP2);
  not not_236 (not_236_out, OP5);
  not not_237 (not_237_out, OP4);
  not not_238 (not_238_out, OP3);
  not not_239 (not_239_out, OP2);
  not not_240 (not_240_out, OP1);
  not not_241 (not_241_out, OP0);
  not not_242 (not_242_out, F4);
  not not_243 (not_243_out, F3);
  not not_244 (not_244_out, F2);
  not not_245 (not_245_out, OP5);
  not not_246 (not_246_out, OP4);
  not not_247 (not_247_out, OP2);
  not not_248 (not_248_out, OP5);
  not not_249 (not_249_out, OP4);
  not not_250 (not_250_out, OP3);
  not not_251 (not_251_out, OP2);
  not not_252 (not_252_out, OP1);
  not not_253 (not_253_out, OP0);
  not not_254 (not_254_out, F4);
  not not_255 (not_255_out, F3);
  not not_256 (not_256_out, F1);
  not not_257 (not_257_out, OP5);
  not not_258 (not_258_out, OP4);
  not not_259 (not_259_out, OP3);
  not not_260 (not_260_out, OP2);
  not not_261 (not_261_out, OP1);
  not not_262 (not_262_out, OP0);
  not not_263 (not_263_out, F4);
  not not_264 (not_264_out, F3);
  not not_265 (not_265_out, OP5);
  not not_266 (not_266_out, OP4);
  not not_267 (not_267_out, OP3);
  not not_268 (not_268_out, OP2);
  not not_269 (not_269_out, OP1);
  not not_270 (not_270_out, OP0);
  not not_271 (not_271_out, F4);
  not not_272 (not_272_out, F2);
  not not_273 (not_273_out, F0);
  not not_274 (not_274_out, OP5);
  not not_275 (not_275_out, OP4);
  not not_276 (not_276_out, OP3);
  not not_277 (not_277_out, OP2);
  not not_278 (not_278_out, OP1);
  not not_279 (not_279_out, OP0);
  not not_280 (not_280_out, F4);
  not not_281 (not_281_out, F2);
  not not_282 (not_282_out, OP5);
  not not_283 (not_283_out, OP4);
  not not_284 (not_284_out, OP2);
  not not_285 (not_285_out, OP0);
  not not_286 (not_286_out, OP5);
  not not_287 (not_287_out, OP4);
  not not_288 (not_288_out, OP1);
  not not_289 (not_289_out, OP5);
  not not_290 (not_290_out, OP4);
  not not_291 (not_291_out, OP3);
  not not_292 (not_292_out, OP2);
  not not_293 (not_293_out, OP1);
  not not_294 (not_294_out, OP0);
  not not_295 (not_295_out, F4);
  not not_296 (not_296_out, F3);
  not not_297 (not_297_out, F0);
  not not_298 (not_298_out, OP5);
  not not_299 (not_299_out, OP4);
  not not_300 (not_300_out, OP0);
  not not_301 (not_301_out, OP5);
  not not_302 (not_302_out, OP4);
  not not_303 (not_303_out, OP2);
  and and_1 (and_1_out, not_1_out, not_2_out, not_3_out, not_4_out, not_5_out, not_6_out, not_7_out, not_8_out, not_9_out, not_10_out, F1, F0);
  and and_2 (and_2_out, not_11_out, not_12_out, not_13_out, not_14_out, not_15_out, not_16_out, F5, not_17_out, not_18_out, not_19_out, not_20_out, not_21_out);
  and and_3 (and_3_out, not_22_out, not_23_out, not_24_out, not_25_out, not_26_out, not_27_out, F5, not_28_out, not_29_out, not_30_out, not_31_out, F0);
  and and_4 (and_4_out, not_32_out, not_33_out, not_34_out, not_35_out, not_36_out, not_37_out, F5, not_38_out, not_39_out, F2, not_40_out, not_41_out);
  and and_5 (and_5_out, not_42_out, not_43_out, not_44_out, not_45_out, not_46_out, not_47_out, F5, not_48_out, F3, not_49_out, F1, not_50_out);
  and and_6 (and_6_out, not_51_out, not_52_out, OP3, not_53_out, not_54_out, not_55_out);
  and and_7 (and_7_out, not_56_out, not_57_out, OP3, OP2, not_58_out, not_59_out);
  and and_8 (and_8_out, not_60_out, not_61_out, OP3, not_62_out, not_63_out, OP0);
  and and_9 (and_9_out, not_64_out, not_65_out, OP3, not_66_out, OP1, not_67_out);
  and and_10 (and_10_out, OP5, not_68_out, not_69_out, not_70_out, OP1, OP0);
  and and_11 (and_11_out, OP5, not_71_out, OP3, not_72_out, OP1, OP0);
  and and_12 (and_12_out, not_73_out, not_74_out, not_75_out, not_76_out, not_77_out, not_78_out, F5, not_79_out, not_80_out, F2, F1, not_81_out);
  and and_13 (and_13_out, not_82_out, not_83_out, not_84_out, not_85_out, not_86_out, not_87_out, not_88_out, not_89_out, not_90_out, F2, F1, F0);
  and and_14 (and_14_out, not_91_out, not_92_out, OP3, OP2, OP1, not_93_out);
  and and_15 (and_15_out, not_94_out, not_95_out, not_96_out, not_97_out, not_98_out, not_99_out, not_100_out, not_101_out, not_102_out, not_103_out, F1, not_104_out);
  and and_16 (and_16_out, not_105_out, not_106_out, not_107_out, not_108_out, not_109_out, not_110_out, F5, not_111_out, not_112_out, not_113_out, F1, not_114_out);
  and and_17 (and_17_out, not_115_out, not_116_out, not_117_out, not_118_out, not_119_out, not_120_out, F5, not_121_out, not_122_out, F2, not_123_out, not_124_out);
  and and_18 (and_18_out, not_125_out, not_126_out, not_127_out, not_128_out, not_129_out, not_130_out, F5, not_131_out, not_132_out, F2, F1, F0);
  and and_19 (and_19_out, not_133_out, not_134_out, not_135_out, not_136_out, not_137_out, not_138_out, F5, not_139_out, F3, not_140_out, F1, not_141_out);
  and and_20 (and_20_out, not_142_out, not_143_out, OP3, OP2, not_144_out, not_145_out);
  and and_21 (and_21_out, not_146_out, not_147_out, OP3, not_148_out, OP1, not_149_out);
  and and_22 (and_22_out, not_150_out, not_151_out, not_152_out, not_153_out, not_154_out, not_155_out, F5, not_156_out, not_157_out, not_158_out, F1, F0);
  and and_23 (and_23_out, not_159_out, not_160_out, not_161_out, not_162_out, not_163_out, not_164_out, not_165_out, not_166_out, not_167_out, F2, F1, not_168_out);
  and and_24 (and_24_out, not_169_out, not_170_out, not_171_out, not_172_out, not_173_out, not_174_out, F5, not_175_out, not_176_out, not_177_out, not_178_out, not_179_out);
  and and_25 (and_25_out, not_180_out, not_181_out, not_182_out, not_183_out, not_184_out, not_185_out, F5, not_186_out, not_187_out, not_188_out, not_189_out, F0);
  and and_26 (and_26_out, not_190_out, not_191_out, not_192_out, not_193_out, not_194_out, not_195_out, F5, not_196_out, not_197_out, not_198_out, F1, not_199_out);
  and and_27 (and_27_out, not_200_out, not_201_out, not_202_out, not_203_out, not_204_out, not_205_out, F5, not_206_out, not_207_out, F2, not_208_out, not_209_out);
  and and_28 (and_28_out, not_210_out, not_211_out, not_212_out, not_213_out, not_214_out, not_215_out, F5, not_216_out, F3, not_217_out, F1, F0);
  and and_29 (and_29_out, not_218_out, not_219_out, OP3, not_220_out, not_221_out, not_222_out);
  and and_30 (and_30_out, not_223_out, not_224_out, OP3, OP2, not_225_out, not_226_out);
  and and_31 (and_31_out, not_227_out, not_228_out, OP3, not_229_out, not_230_out, OP0);
  and and_32 (and_32_out, OP5, not_231_out, not_232_out, not_233_out, OP1, OP0);
  and and_33 (and_33_out, OP5, not_234_out, OP3, not_235_out, OP1, OP0);
  and and_34 (and_34_out, not_236_out, not_237_out, not_238_out, not_239_out, not_240_out, not_241_out, F5, not_242_out, not_243_out, not_244_out, F1, F0);
  and and_35 (and_35_out, not_245_out, not_246_out, OP3, not_247_out, OP1, OP0);
  and and_36 (and_36_out, not_248_out, not_249_out, not_250_out, not_251_out, not_252_out, not_253_out, F5, not_254_out, not_255_out, F2, not_256_out, F0);
  and and_37 (and_37_out, not_257_out, not_258_out, not_259_out, not_260_out, not_261_out, not_262_out, F5, not_263_out, not_264_out, F2, F1, F0);
  and and_38 (and_38_out, not_265_out, not_266_out, not_267_out, not_268_out, not_269_out, not_270_out, F5, not_271_out, F3, not_272_out, F1, not_273_out);
  and and_39 (and_39_out, not_274_out, not_275_out, not_276_out, not_277_out, not_278_out, not_279_out, F5, not_280_out, F3, not_281_out, F1, F0);
  and and_40 (and_40_out, not_282_out, not_283_out, OP3, not_284_out, OP1, not_285_out);
  and and_41 (and_41_out, not_286_out, not_287_out, OP3, OP2, not_288_out, OP0);
  and and_42 (and_42_out, not_289_out, not_290_out, not_291_out, not_292_out, not_293_out, not_294_out, F5, not_295_out, not_296_out, F2, F1, not_297_out);
  and and_43 (and_43_out, not_298_out, not_299_out, OP3, OP2, OP1, not_300_out);
  and and_44 (and_44_out, not_301_out, not_302_out, OP3, not_303_out, OP1, OP0);
  or or_1 (S1, and_15_out, and_16_out, and_17_out, and_18_out, and_19_out, and_20_out, and_21_out, and_22_out, and_23_out);
  or or_2 (S3, and_36_out, and_37_out, and_38_out, and_39_out, and_40_out, and_41_out, and_42_out, and_43_out, and_44_out);
  or or_3 (S0, and_1_out, and_2_out, and_3_out, and_4_out, and_5_out, and_6_out, and_7_out, and_8_out, and_9_out, and_10_out, and_11_out, and_12_out, and_13_out, and_14_out);
  or or_4 (S2, and_24_out, and_25_out, and_26_out, and_27_out, and_28_out, and_29_out, and_30_out, and_31_out, and_32_out, and_33_out, and_34_out, and_35_out);
endmodule

module \控制信号生成  (
  input  OP0,
  input  OP1,
  input  OP2,
  input  OP3,
  input  OP4,
  input  OP5,
  input  F0,
  input  F1,
  input  F2,
  input  F3,
  input  F4,
  input  F5,
  output MemToReg,
  output MemWrite,
  output ALU_SRC,
  output RegWrite,
  output SysCALL,
  output SignedExt,
  output RegDst,
  output BEQ,
  output BNE,
  output JR,
  output JMP,
  output JAL
);

  wire and_3_out, and_4_out, and_5_out, and_6_out, and_7_out, and_8_out, and_9_out, and_10_out, and_11_out,
       and_12_out, and_13_out, and_14_out, and_15_out, and_16_out, and_17_out, and_18_out, and_19_out,
       and_20_out, and_21_out, and_22_out, and_23_out, and_24_out, and_25_out, and_26_out, and_27_out,
       and_28_out, and_29_out, and_30_out, and_31_out, and_32_out, and_33_out, and_34_out, and_35_out,
       and_36_out, and_38_out, and_39_out, and_40_out, and_41_out, and_42_out, and_43_out, and_44_out,
       and_45_out, and_46_out, and_47_out, and_48_out, and_49_out, and_50_out, and_51_out, and_52_out,
       and_53_out, and_54_out, and_55_out, and_56_out, and_57_out, and_58_out, and_59_out, not_1_out,
       not_2_out, not_3_out, not_4_out, not_5_out, not_6_out, not_7_out, not_8_out, not_9_out, not_10_out,
       not_11_out, not_12_out, not_13_out, not_14_out, not_15_out, not_16_out, not_17_out, not_18_out,
       not_19_out, not_20_out, not_21_out, not_22_out, not_23_out, not_24_out, not_25_out, not_26_out,
       not_27_out, not_28_out, not_29_out, not_30_out, not_31_out, not_32_out, not_33_out, not_34_out,
       not_35_out, not_36_out, not_37_out, not_38_out, not_39_out, not_40_out, not_41_out, not_42_out,
       not_43_out, not_44_out, not_45_out, not_46_out, not_47_out, not_48_out, not_49_out, not_50_out,
       not_51_out, not_52_out, not_53_out, not_54_out, not_55_out, not_56_out, not_57_out, not_58_out,
       not_59_out, not_60_out, not_61_out, not_62_out, not_63_out, not_64_out, not_65_out, not_66_out,
       not_67_out, not_68_out, not_69_out, not_70_out, not_71_out, not_72_out, not_73_out, not_74_out,
       not_75_out, not_76_out, not_77_out, not_78_out, not_79_out, not_80_out, not_81_out, not_82_out,
       not_83_out, not_84_out, not_85_out, not_86_out, not_87_out, not_88_out, not_89_out, not_90_out,
       not_91_out, not_92_out, not_93_out, not_94_out, not_95_out, not_96_out, not_97_out, not_98_out,
       not_99_out, not_100_out, not_101_out, not_102_out, not_103_out, not_104_out, not_105_out, not_106_out,
       not_107_out, not_108_out, not_109_out, not_110_out, not_111_out, not_112_out, not_113_out,
       not_114_out, not_115_out, not_116_out, not_117_out, not_118_out, not_119_out, not_120_out,
       not_121_out, not_122_out, not_123_out, not_124_out, not_125_out, not_126_out, not_127_out,
       not_128_out, not_129_out, not_130_out, not_131_out, not_132_out, not_133_out, not_134_out,
       not_135_out, not_136_out, not_137_out, not_138_out, not_139_out, not_140_out, not_141_out,
       not_142_out, not_143_out, not_144_out, not_145_out, not_146_out, not_147_out, not_148_out,
       not_149_out, not_150_out, not_151_out, not_152_out, not_153_out, not_154_out, not_155_out,
       not_156_out, not_157_out, not_158_out, not_159_out, not_160_out, not_161_out, not_162_out,
       not_163_out, not_164_out, not_165_out, not_166_out, not_167_out, not_168_out, not_169_out,
       not_170_out, not_171_out, not_172_out, not_173_out, not_174_out, not_175_out, not_176_out,
       not_177_out, not_178_out, not_179_out, not_180_out, not_181_out, not_182_out, not_183_out,
       not_184_out, not_185_out, not_186_out, not_187_out, not_188_out, not_189_out, not_190_out,
       not_191_out, not_192_out, not_193_out, not_194_out, not_195_out, not_196_out, not_197_out,
       not_198_out, not_199_out, not_200_out, not_201_out, not_202_out, not_203_out, not_204_out,
       not_205_out, not_206_out, not_207_out, not_208_out, not_209_out, not_210_out, not_211_out,
       not_212_out, not_213_out, not_214_out, not_215_out, not_216_out, not_217_out, not_218_out,
       not_219_out, not_220_out, not_221_out, not_222_out, not_223_out, not_224_out, not_225_out,
       not_226_out, not_227_out, not_228_out, not_229_out, not_230_out, not_231_out, not_232_out,
       not_233_out, not_234_out, not_235_out, not_236_out, not_237_out, not_238_out, not_239_out,
       not_240_out, not_241_out, not_242_out, not_243_out, not_244_out, not_245_out, not_246_out,
       not_247_out, not_248_out, not_249_out, not_250_out, not_251_out, not_252_out, not_253_out,
       not_254_out, not_255_out, not_256_out, not_257_out, not_258_out, not_259_out, not_260_out,
       not_261_out, not_262_out, not_263_out, not_264_out, not_265_out, not_266_out, not_267_out,
       not_268_out, not_269_out, not_270_out, not_271_out, not_272_out, not_273_out, not_274_out,
       not_275_out, not_276_out, not_277_out, not_278_out, not_279_out, not_280_out, not_281_out,
       not_282_out, not_283_out, not_284_out, not_285_out, not_286_out, not_287_out, not_288_out,
       not_289_out, not_290_out, not_291_out, not_292_out, not_293_out, not_294_out, not_295_out,
       not_296_out, not_297_out, not_298_out, not_299_out, not_300_out, not_301_out, not_302_out,
       not_303_out, not_304_out, not_305_out, not_306_out, not_307_out, not_308_out, not_309_out,
       not_310_out, not_311_out, not_312_out, not_313_out, not_314_out, not_315_out, not_316_out,
       not_317_out, not_318_out, not_319_out, not_320_out, not_321_out, not_322_out, not_323_out,
       not_324_out, not_325_out, not_326_out, not_327_out, not_328_out, not_329_out, not_330_out,
       not_331_out, not_332_out, not_333_out, not_334_out, not_335_out, not_336_out, not_337_out,
       not_338_out, not_339_out, not_340_out, not_341_out, not_342_out, not_343_out, not_344_out,
       not_345_out, not_346_out, not_347_out, not_348_out, not_349_out, not_350_out, not_351_out,
       not_352_out, not_353_out, not_354_out, not_355_out, not_356_out, not_357_out, not_358_out,
       not_359_out, not_360_out, not_361_out, not_362_out, not_363_out, not_364_out, not_365_out,
       not_366_out, not_367_out, not_368_out, not_369_out, not_370_out, not_371_out, not_372_out,
       not_373_out, not_374_out, not_375_out, not_376_out, not_377_out, not_378_out, not_379_out,
       not_380_out, not_381_out, not_382_out, not_383_out, not_384_out, not_385_out, not_386_out,
       not_387_out, not_388_out, not_389_out, not_390_out, not_391_out, not_392_out, not_393_out,
       not_394_out, not_395_out, not_396_out, not_397_out, not_398_out, not_399_out, not_400_out,
       not_401_out, not_402_out, not_403_out, not_404_out, not_405_out, not_406_out, not_407_out,
       not_408_out, not_409_out, not_410_out, not_411_out, not_412_out, not_413_out, not_414_out,
       not_415_out, not_416_out, not_417_out, not_418_out, not_419_out, not_420_out, not_421_out,
       not_422_out, not_423_out, not_424_out, not_425_out, not_426_out, not_427_out, not_428_out,
       not_429_out, not_430_out, not_431_out, not_432_out, not_433_out, not_434_out, not_435_out,
       not_436_out, not_437_out, not_438_out, not_439_out, not_440_out, not_441_out;

  not not_1 (not_1_out, OP4);
  not not_2 (not_2_out, OP3);
  not not_3 (not_3_out, OP2);
  not not_4 (not_4_out, OP4);
  not not_5 (not_5_out, OP2);
  not not_6 (not_6_out, OP5);
  not not_7 (not_7_out, OP4);
  not not_8 (not_8_out, OP2);
  not not_9 (not_9_out, OP1);
  not not_10 (not_10_out, OP0);
  not not_11 (not_11_out, OP5);
  not not_12 (not_12_out, OP4);
  not not_13 (not_13_out, OP1);
  not not_14 (not_14_out, OP0);
  not not_15 (not_15_out, OP5);
  not not_16 (not_16_out, OP4);
  not not_17 (not_17_out, OP2);
  not not_18 (not_18_out, OP1);
  not not_19 (not_19_out, OP5);
  not not_20 (not_20_out, OP4);
  not not_21 (not_21_out, OP2);
  not not_22 (not_22_out, OP0);
  not not_23 (not_23_out, OP5);
  not not_24 (not_24_out, OP4);
  not not_25 (not_25_out, OP1);
  not not_26 (not_26_out, OP4);
  not not_27 (not_27_out, OP3);
  not not_28 (not_28_out, OP2);
  not not_29 (not_29_out, OP4);
  not not_30 (not_30_out, OP2);
  not not_31 (not_31_out, OP5);
  not not_32 (not_32_out, OP4);
  not not_33 (not_33_out, OP0);
  not not_34 (not_34_out, OP5);
  not not_35 (not_35_out, OP4);
  not not_36 (not_36_out, OP2);
  not not_37 (not_37_out, OP5);
  not not_38 (not_38_out, OP4);
  not not_39 (not_39_out, OP3);
  not not_40 (not_40_out, OP2);
  not not_41 (not_41_out, OP1);
  not not_42 (not_42_out, OP0);
  not not_43 (not_43_out, F5);
  not not_44 (not_44_out, F4);
  not not_45 (not_45_out, F3);
  not not_46 (not_46_out, F2);
  not not_47 (not_47_out, F1);
  not not_48 (not_48_out, F0);
  not not_49 (not_49_out, OP5);
  not not_50 (not_50_out, OP4);
  not not_51 (not_51_out, OP3);
  not not_52 (not_52_out, OP2);
  not not_53 (not_53_out, OP1);
  not not_54 (not_54_out, OP0);
  not not_55 (not_55_out, F5);
  not not_56 (not_56_out, F4);
  not not_57 (not_57_out, F3);
  not not_58 (not_58_out, F2);
  not not_59 (not_59_out, OP5);
  not not_60 (not_60_out, OP4);
  not not_61 (not_61_out, OP3);
  not not_62 (not_62_out, OP2);
  not not_63 (not_63_out, OP1);
  not not_64 (not_64_out, OP0);
  not not_65 (not_65_out, F5);
  not not_66 (not_66_out, F4);
  not not_67 (not_67_out, F3);
  not not_68 (not_68_out, F2);
  not not_69 (not_69_out, F0);
  not not_70 (not_70_out, OP5);
  not not_71 (not_71_out, OP4);
  not not_72 (not_72_out, OP3);
  not not_73 (not_73_out, OP2);
  not not_74 (not_74_out, OP1);
  not not_75 (not_75_out, OP0);
  not not_76 (not_76_out, F4);
  not not_77 (not_77_out, F3);
  not not_78 (not_78_out, F2);
  not not_79 (not_79_out, F1);
  not not_80 (not_80_out, F0);
  not not_81 (not_81_out, OP5);
  not not_82 (not_82_out, OP4);
  not not_83 (not_83_out, OP3);
  not not_84 (not_84_out, OP2);
  not not_85 (not_85_out, OP1);
  not not_86 (not_86_out, OP0);
  not not_87 (not_87_out, F4);
  not not_88 (not_88_out, F3);
  not not_89 (not_89_out, F2);
  not not_90 (not_90_out, F1);
  not not_91 (not_91_out, OP5);
  not not_92 (not_92_out, OP4);
  not not_93 (not_93_out, OP3);
  not not_94 (not_94_out, OP2);
  not not_95 (not_95_out, OP1);
  not not_96 (not_96_out, OP0);
  not not_97 (not_97_out, F4);
  not not_98 (not_98_out, F3);
  not not_99 (not_99_out, F2);
  not not_100 (not_100_out, F0);
  not not_101 (not_101_out, OP5);
  not not_102 (not_102_out, OP4);
  not not_103 (not_103_out, OP3);
  not not_104 (not_104_out, OP2);
  not not_105 (not_105_out, OP1);
  not not_106 (not_106_out, OP0);
  not not_107 (not_107_out, F4);
  not not_108 (not_108_out, F3);
  not not_109 (not_109_out, F1);
  not not_110 (not_110_out, F0);
  not not_111 (not_111_out, OP5);
  not not_112 (not_112_out, OP4);
  not not_113 (not_113_out, OP3);
  not not_114 (not_114_out, OP2);
  not not_115 (not_115_out, OP1);
  not not_116 (not_116_out, OP0);
  not not_117 (not_117_out, F4);
  not not_118 (not_118_out, F3);
  not not_119 (not_119_out, F1);
  not not_120 (not_120_out, OP5);
  not not_121 (not_121_out, OP4);
  not not_122 (not_122_out, OP3);
  not not_123 (not_123_out, OP2);
  not not_124 (not_124_out, OP1);
  not not_125 (not_125_out, OP0);
  not not_126 (not_126_out, F4);
  not not_127 (not_127_out, F3);
  not not_128 (not_128_out, OP5);
  not not_129 (not_129_out, OP4);
  not not_130 (not_130_out, OP3);
  not not_131 (not_131_out, OP2);
  not not_132 (not_132_out, OP1);
  not not_133 (not_133_out, OP0);
  not not_134 (not_134_out, F4);
  not not_135 (not_135_out, F2);
  not not_136 (not_136_out, F0);
  not not_137 (not_137_out, OP5);
  not not_138 (not_138_out, OP4);
  not not_139 (not_139_out, OP3);
  not not_140 (not_140_out, OP2);
  not not_141 (not_141_out, OP1);
  not not_142 (not_142_out, OP0);
  not not_143 (not_143_out, F4);
  not not_144 (not_144_out, F2);
  not not_145 (not_145_out, OP5);
  not not_146 (not_146_out, OP4);
  not not_147 (not_147_out, OP3);
  not not_148 (not_148_out, OP2);
  not not_149 (not_149_out, OP5);
  not not_150 (not_150_out, OP4);
  not not_151 (not_151_out, OP2);
  not not_152 (not_152_out, OP1);
  not not_153 (not_153_out, OP0);
  not not_154 (not_154_out, OP5);
  not not_155 (not_155_out, OP4);
  not not_156 (not_156_out, OP1);
  not not_157 (not_157_out, OP0);
  not not_158 (not_158_out, OP5);
  not not_159 (not_159_out, OP4);
  not not_160 (not_160_out, OP2);
  not not_161 (not_161_out, OP1);
  not not_162 (not_162_out, OP5);
  not not_163 (not_163_out, OP4);
  not not_164 (not_164_out, OP2);
  not not_165 (not_165_out, OP0);
  not not_166 (not_166_out, OP5);
  not not_167 (not_167_out, OP4);
  not not_168 (not_168_out, OP1);
  not not_169 (not_169_out, OP4);
  not not_170 (not_170_out, OP3);
  not not_171 (not_171_out, OP2);
  not not_172 (not_172_out, OP5);
  not not_173 (not_173_out, OP4);
  not not_174 (not_174_out, OP3);
  not not_175 (not_175_out, OP2);
  not not_176 (not_176_out, OP1);
  not not_177 (not_177_out, OP0);
  not not_178 (not_178_out, F4);
  not not_179 (not_179_out, F3);
  not not_180 (not_180_out, F2);
  not not_181 (not_181_out, OP5);
  not not_182 (not_182_out, OP4);
  not not_183 (not_183_out, OP3);
  not not_184 (not_184_out, OP2);
  not not_185 (not_185_out, OP1);
  not not_186 (not_186_out, OP0);
  not not_187 (not_187_out, F4);
  not not_188 (not_188_out, F3);
  not not_189 (not_189_out, F0);
  not not_190 (not_190_out, OP5);
  not not_191 (not_191_out, OP4);
  not not_192 (not_192_out, OP3);
  not not_193 (not_193_out, OP2);
  not not_194 (not_194_out, OP1);
  not not_195 (not_195_out, OP0);
  not not_196 (not_196_out, F5);
  not not_197 (not_197_out, F4);
  not not_198 (not_198_out, F3);
  not not_199 (not_199_out, F1);
  not not_200 (not_200_out, F0);
  not not_201 (not_201_out, OP5);
  not not_202 (not_202_out, OP4);
  not not_203 (not_203_out, OP3);
  not not_204 (not_204_out, OP2);
  not not_205 (not_205_out, OP1);
  not not_206 (not_206_out, OP0);
  not not_207 (not_207_out, F5);
  not not_208 (not_208_out, F4);
  not not_209 (not_209_out, F3);
  not not_210 (not_210_out, F0);
  not not_211 (not_211_out, OP5);
  not not_212 (not_212_out, OP4);
  not not_213 (not_213_out, OP3);
  not not_214 (not_214_out, OP2);
  not not_215 (not_215_out, OP1);
  not not_216 (not_216_out, OP0);
  not not_217 (not_217_out, F5);
  not not_218 (not_218_out, F4);
  not not_219 (not_219_out, F3);
  not not_220 (not_220_out, OP5);
  not not_221 (not_221_out, OP4);
  not not_222 (not_222_out, OP0);
  not not_223 (not_223_out, OP5);
  not not_224 (not_224_out, OP4);
  not not_225 (not_225_out, OP2);
  not not_226 (not_226_out, OP5);
  not not_227 (not_227_out, OP4);
  not not_228 (not_228_out, OP3);
  not not_229 (not_229_out, OP2);
  not not_230 (not_230_out, OP1);
  not not_231 (not_231_out, OP0);
  not not_232 (not_232_out, F5);
  not not_233 (not_233_out, F4);
  not not_234 (not_234_out, F1);
  not not_235 (not_235_out, F0);
  not not_236 (not_236_out, OP5);
  not not_237 (not_237_out, OP4);
  not not_238 (not_238_out, OP2);
  not not_239 (not_239_out, OP1);
  not not_240 (not_240_out, OP0);
  not not_241 (not_241_out, OP5);
  not not_242 (not_242_out, OP4);
  not not_243 (not_243_out, OP2);
  not not_244 (not_244_out, OP1);
  not not_245 (not_245_out, OP5);
  not not_246 (not_246_out, OP4);
  not not_247 (not_247_out, OP2);
  not not_248 (not_248_out, OP0);
  not not_249 (not_249_out, OP4);
  not not_250 (not_250_out, OP3);
  not not_251 (not_251_out, OP2);
  not not_252 (not_252_out, OP4);
  not not_253 (not_253_out, OP2);
  not not_254 (not_254_out, OP5);
  not not_255 (not_255_out, OP4);
  not not_256 (not_256_out, OP2);
  not not_257 (not_257_out, OP5);
  not not_258 (not_258_out, OP4);
  not not_259 (not_259_out, OP3);
  not not_260 (not_260_out, OP2);
  not not_261 (not_261_out, OP1);
  not not_262 (not_262_out, OP0);
  not not_263 (not_263_out, F5);
  not not_264 (not_264_out, F4);
  not not_265 (not_265_out, F3);
  not not_266 (not_266_out, F2);
  not not_267 (not_267_out, F1);
  not not_268 (not_268_out, F0);
  not not_269 (not_269_out, OP5);
  not not_270 (not_270_out, OP4);
  not not_271 (not_271_out, OP3);
  not not_272 (not_272_out, OP2);
  not not_273 (not_273_out, OP1);
  not not_274 (not_274_out, OP0);
  not not_275 (not_275_out, F5);
  not not_276 (not_276_out, F4);
  not not_277 (not_277_out, F3);
  not not_278 (not_278_out, F2);
  not not_279 (not_279_out, OP5);
  not not_280 (not_280_out, OP4);
  not not_281 (not_281_out, OP3);
  not not_282 (not_282_out, OP2);
  not not_283 (not_283_out, OP1);
  not not_284 (not_284_out, OP0);
  not not_285 (not_285_out, F5);
  not not_286 (not_286_out, F4);
  not not_287 (not_287_out, F3);
  not not_288 (not_288_out, F2);
  not not_289 (not_289_out, F0);
  not not_290 (not_290_out, OP5);
  not not_291 (not_291_out, OP4);
  not not_292 (not_292_out, OP3);
  not not_293 (not_293_out, OP2);
  not not_294 (not_294_out, OP1);
  not not_295 (not_295_out, OP0);
  not not_296 (not_296_out, F4);
  not not_297 (not_297_out, F3);
  not not_298 (not_298_out, F2);
  not not_299 (not_299_out, F1);
  not not_300 (not_300_out, F0);
  not not_301 (not_301_out, OP5);
  not not_302 (not_302_out, OP4);
  not not_303 (not_303_out, OP3);
  not not_304 (not_304_out, OP2);
  not not_305 (not_305_out, OP1);
  not not_306 (not_306_out, OP0);
  not not_307 (not_307_out, F4);
  not not_308 (not_308_out, F3);
  not not_309 (not_309_out, F2);
  not not_310 (not_310_out, F1);
  not not_311 (not_311_out, OP5);
  not not_312 (not_312_out, OP4);
  not not_313 (not_313_out, OP3);
  not not_314 (not_314_out, OP2);
  not not_315 (not_315_out, OP1);
  not not_316 (not_316_out, OP0);
  not not_317 (not_317_out, F4);
  not not_318 (not_318_out, F3);
  not not_319 (not_319_out, F2);
  not not_320 (not_320_out, F0);
  not not_321 (not_321_out, OP5);
  not not_322 (not_322_out, OP4);
  not not_323 (not_323_out, OP3);
  not not_324 (not_324_out, OP2);
  not not_325 (not_325_out, OP1);
  not not_326 (not_326_out, OP0);
  not not_327 (not_327_out, F4);
  not not_328 (not_328_out, F3);
  not not_329 (not_329_out, F1);
  not not_330 (not_330_out, F0);
  not not_331 (not_331_out, OP5);
  not not_332 (not_332_out, OP4);
  not not_333 (not_333_out, OP3);
  not not_334 (not_334_out, OP2);
  not not_335 (not_335_out, OP1);
  not not_336 (not_336_out, OP0);
  not not_337 (not_337_out, F4);
  not not_338 (not_338_out, F3);
  not not_339 (not_339_out, F1);
  not not_340 (not_340_out, OP5);
  not not_341 (not_341_out, OP4);
  not not_342 (not_342_out, OP3);
  not not_343 (not_343_out, OP2);
  not not_344 (not_344_out, OP1);
  not not_345 (not_345_out, OP0);
  not not_346 (not_346_out, F4);
  not not_347 (not_347_out, F3);
  not not_348 (not_348_out, OP5);
  not not_349 (not_349_out, OP4);
  not not_350 (not_350_out, OP3);
  not not_351 (not_351_out, OP2);
  not not_352 (not_352_out, OP1);
  not not_353 (not_353_out, OP0);
  not not_354 (not_354_out, F4);
  not not_355 (not_355_out, F2);
  not not_356 (not_356_out, F0);
  not not_357 (not_357_out, OP5);
  not not_358 (not_358_out, OP4);
  not not_359 (not_359_out, OP3);
  not not_360 (not_360_out, OP2);
  not not_361 (not_361_out, OP1);
  not not_362 (not_362_out, OP0);
  not not_363 (not_363_out, F4);
  not not_364 (not_364_out, F2);
  not not_365 (not_365_out, OP5);
  not not_366 (not_366_out, OP4);
  not not_367 (not_367_out, OP3);
  not not_368 (not_368_out, OP2);
  not not_369 (not_369_out, OP1);
  not not_370 (not_370_out, OP0);
  not not_371 (not_371_out, F4);
  not not_372 (not_372_out, F3);
  not not_373 (not_373_out, F2);
  not not_374 (not_374_out, OP5);
  not not_375 (not_375_out, OP4);
  not not_376 (not_376_out, OP3);
  not not_377 (not_377_out, OP2);
  not not_378 (not_378_out, OP1);
  not not_379 (not_379_out, OP0);
  not not_380 (not_380_out, F4);
  not not_381 (not_381_out, F3);
  not not_382 (not_382_out, F0);
  not not_383 (not_383_out, OP5);
  not not_384 (not_384_out, OP4);
  not not_385 (not_385_out, OP3);
  not not_386 (not_386_out, OP2);
  not not_387 (not_387_out, OP1);
  not not_388 (not_388_out, OP0);
  not not_389 (not_389_out, F5);
  not not_390 (not_390_out, F4);
  not not_391 (not_391_out, F3);
  not not_392 (not_392_out, F1);
  not not_393 (not_393_out, F0);
  not not_394 (not_394_out, OP5);
  not not_395 (not_395_out, OP4);
  not not_396 (not_396_out, OP3);
  not not_397 (not_397_out, OP2);
  not not_398 (not_398_out, OP1);
  not not_399 (not_399_out, OP0);
  not not_400 (not_400_out, F5);
  not not_401 (not_401_out, F4);
  not not_402 (not_402_out, F3);
  not not_403 (not_403_out, F0);
  not not_404 (not_404_out, OP5);
  not not_405 (not_405_out, OP4);
  not not_406 (not_406_out, OP3);
  not not_407 (not_407_out, OP2);
  not not_408 (not_408_out, OP1);
  not not_409 (not_409_out, OP0);
  not not_410 (not_410_out, F5);
  not not_411 (not_411_out, F4);
  not not_412 (not_412_out, F3);
  not not_413 (not_413_out, OP5);
  not not_414 (not_414_out, OP4);
  not not_415 (not_415_out, OP3);
  not not_416 (not_416_out, OP1);
  not not_417 (not_417_out, OP0);
  not not_418 (not_418_out, OP5);
  not not_419 (not_419_out, OP4);
  not not_420 (not_420_out, OP3);
  not not_421 (not_421_out, OP1);
  not not_422 (not_422_out, OP5);
  not not_423 (not_423_out, OP4);
  not not_424 (not_424_out, OP3);
  not not_425 (not_425_out, OP2);
  not not_426 (not_426_out, OP1);
  not not_427 (not_427_out, OP0);
  not not_428 (not_428_out, F5);
  not not_429 (not_429_out, F4);
  not not_430 (not_430_out, F2);
  not not_431 (not_431_out, F1);
  not not_432 (not_432_out, F0);
  not not_433 (not_433_out, OP5);
  not not_434 (not_434_out, OP4);
  not not_435 (not_435_out, OP3);
  not not_436 (not_436_out, OP2);
  not not_437 (not_437_out, OP0);
  not not_438 (not_438_out, OP5);
  not not_439 (not_439_out, OP4);
  not not_440 (not_440_out, OP3);
  not not_441 (not_441_out, OP2);
  and and_1 (MemToReg, OP5, not_1_out, not_2_out, not_3_out, OP1, OP0);
  and and_2 (MemWrite, OP5, not_4_out, OP3, not_5_out, OP1, OP0);
  and and_3 (and_3_out, not_6_out, not_7_out, OP3, not_8_out, not_9_out, not_10_out);
  and and_4 (and_4_out, not_11_out, not_12_out, OP3, OP2, not_13_out, not_14_out);
  and and_5 (and_5_out, not_15_out, not_16_out, OP3, not_17_out, not_18_out, OP0);
  and and_6 (and_6_out, not_19_out, not_20_out, OP3, not_21_out, OP1, not_22_out);
  and and_7 (and_7_out, not_23_out, not_24_out, OP3, OP2, not_25_out, OP0);
  and and_8 (and_8_out, OP5, not_26_out, not_27_out, not_28_out, OP1, OP0);
  and and_9 (and_9_out, OP5, not_29_out, OP3, not_30_out, OP1, OP0);
  and and_10 (and_10_out, not_31_out, not_32_out, OP3, OP2, OP1, not_33_out);
  and and_11 (and_11_out, not_34_out, not_35_out, OP3, not_36_out, OP1, OP0);
  and and_12 (and_12_out, not_37_out, not_38_out, not_39_out, not_40_out, not_41_out, not_42_out, not_43_out, not_44_out, not_45_out, not_46_out, not_47_out, not_48_out);
  and and_13 (and_13_out, not_49_out, not_50_out, not_51_out, not_52_out, not_53_out, not_54_out, not_55_out, not_56_out, not_57_out, not_58_out, F1, F0);
  and and_14 (and_14_out, not_59_out, not_60_out, not_61_out, not_62_out, not_63_out, not_64_out, not_65_out, not_66_out, not_67_out, not_68_out, F1, not_69_out);
  and and_15 (and_15_out, not_70_out, not_71_out, not_72_out, not_73_out, not_74_out, not_75_out, F5, not_76_out, not_77_out, not_78_out, not_79_out, not_80_out);
  and and_16 (and_16_out, not_81_out, not_82_out, not_83_out, not_84_out, not_85_out, not_86_out, F5, not_87_out, not_88_out, not_89_out, not_90_out, F0);
  and and_17 (and_17_out, not_91_out, not_92_out, not_93_out, not_94_out, not_95_out, not_96_out, F5, not_97_out, not_98_out, not_99_out, F1, not_100_out);
  and and_18 (and_18_out, not_101_out, not_102_out, not_103_out, not_104_out, not_105_out, not_106_out, F5, not_107_out, not_108_out, F2, not_109_out, not_110_out);
  and and_19 (and_19_out, not_111_out, not_112_out, not_113_out, not_114_out, not_115_out, not_116_out, F5, not_117_out, not_118_out, F2, not_119_out, F0);
  and and_20 (and_20_out, not_120_out, not_121_out, not_122_out, not_123_out, not_124_out, not_125_out, F5, not_126_out, not_127_out, F2, F1, F0);
  and and_21 (and_21_out, not_128_out, not_129_out, not_130_out, not_131_out, not_132_out, not_133_out, F5, not_134_out, F3, not_135_out, F1, not_136_out);
  and and_22 (and_22_out, not_137_out, not_138_out, not_139_out, not_140_out, not_141_out, not_142_out, F5, not_143_out, F3, not_144_out, F1, F0);
  and and_23 (and_23_out, not_145_out, not_146_out, not_147_out, not_148_out, OP1, OP0);
  and and_24 (and_24_out, not_149_out, not_150_out, OP3, not_151_out, not_152_out, not_153_out);
  and and_25 (and_25_out, not_154_out, not_155_out, OP3, OP2, not_156_out, not_157_out);
  and and_26 (and_26_out, not_158_out, not_159_out, OP3, not_160_out, not_161_out, OP0);
  and and_27 (and_27_out, not_162_out, not_163_out, OP3, not_164_out, OP1, not_165_out);
  and and_28 (and_28_out, not_166_out, not_167_out, OP3, OP2, not_168_out, OP0);
  and and_29 (and_29_out, OP5, not_169_out, not_170_out, not_171_out, OP1, OP0);
  and and_30 (and_30_out, not_172_out, not_173_out, not_174_out, not_175_out, not_176_out, not_177_out, F5, not_178_out, not_179_out, not_180_out, F1, F0);
  and and_31 (and_31_out, not_181_out, not_182_out, not_183_out, not_184_out, not_185_out, not_186_out, F5, not_187_out, not_188_out, F2, F1, not_189_out);
  and and_32 (and_32_out, not_190_out, not_191_out, not_192_out, not_193_out, not_194_out, not_195_out, not_196_out, not_197_out, not_198_out, F2, not_199_out, not_200_out);
  and and_33 (and_33_out, not_201_out, not_202_out, not_203_out, not_204_out, not_205_out, not_206_out, not_207_out, not_208_out, not_209_out, F2, F1, not_210_out);
  and and_34 (and_34_out, not_211_out, not_212_out, not_213_out, not_214_out, not_215_out, not_216_out, not_217_out, not_218_out, not_219_out, F2, F1, F0);
  and and_35 (and_35_out, not_220_out, not_221_out, OP3, OP2, OP1, not_222_out);
  and and_36 (and_36_out, not_223_out, not_224_out, OP3, not_225_out, OP1, OP0);
  and and_37 (SysCALL, not_226_out, not_227_out, not_228_out, not_229_out, not_230_out, not_231_out, not_232_out, not_233_out, F3, F2, not_234_out, not_235_out);
  and and_38 (and_38_out, not_236_out, not_237_out, OP3, not_238_out, not_239_out, not_240_out);
  and and_39 (and_39_out, not_241_out, not_242_out, OP3, not_243_out, not_244_out, OP0);
  and and_40 (and_40_out, not_245_out, not_246_out, OP3, not_247_out, OP1, not_248_out);
  and and_41 (and_41_out, OP5, not_249_out, not_250_out, not_251_out, OP1, OP0);
  and and_42 (and_42_out, OP5, not_252_out, OP3, not_253_out, OP1, OP0);
  and and_43 (and_43_out, not_254_out, not_255_out, OP3, not_256_out, OP1, OP0);
  and and_44 (and_44_out, not_257_out, not_258_out, not_259_out, not_260_out, not_261_out, not_262_out, not_263_out, not_264_out, not_265_out, not_266_out, not_267_out, not_268_out);
  and and_45 (and_45_out, not_269_out, not_270_out, not_271_out, not_272_out, not_273_out, not_274_out, not_275_out, not_276_out, not_277_out, not_278_out, F1, F0);
  and and_46 (and_46_out, not_279_out, not_280_out, not_281_out, not_282_out, not_283_out, not_284_out, not_285_out, not_286_out, not_287_out, not_288_out, F1, not_289_out);
  and and_47 (and_47_out, not_290_out, not_291_out, not_292_out, not_293_out, not_294_out, not_295_out, F5, not_296_out, not_297_out, not_298_out, not_299_out, not_300_out);
  and and_48 (and_48_out, not_301_out, not_302_out, not_303_out, not_304_out, not_305_out, not_306_out, F5, not_307_out, not_308_out, not_309_out, not_310_out, F0);
  and and_49 (and_49_out, not_311_out, not_312_out, not_313_out, not_314_out, not_315_out, not_316_out, F5, not_317_out, not_318_out, not_319_out, F1, not_320_out);
  and and_50 (and_50_out, not_321_out, not_322_out, not_323_out, not_324_out, not_325_out, not_326_out, F5, not_327_out, not_328_out, F2, not_329_out, not_330_out);
  and and_51 (and_51_out, not_331_out, not_332_out, not_333_out, not_334_out, not_335_out, not_336_out, F5, not_337_out, not_338_out, F2, not_339_out, F0);
  and and_52 (and_52_out, not_340_out, not_341_out, not_342_out, not_343_out, not_344_out, not_345_out, F5, not_346_out, not_347_out, F2, F1, F0);
  and and_53 (and_53_out, not_348_out, not_349_out, not_350_out, not_351_out, not_352_out, not_353_out, F5, not_354_out, F3, not_355_out, F1, not_356_out);
  and and_54 (and_54_out, not_357_out, not_358_out, not_359_out, not_360_out, not_361_out, not_362_out, F5, not_363_out, F3, not_364_out, F1, F0);
  and and_55 (and_55_out, not_365_out, not_366_out, not_367_out, not_368_out, not_369_out, not_370_out, F5, not_371_out, not_372_out, not_373_out, F1, F0);
  and and_56 (and_56_out, not_374_out, not_375_out, not_376_out, not_377_out, not_378_out, not_379_out, F5, not_380_out, not_381_out, F2, F1, not_382_out);
  and and_57 (and_57_out, not_383_out, not_384_out, not_385_out, not_386_out, not_387_out, not_388_out, not_389_out, not_390_out, not_391_out, F2, not_392_out, not_393_out);
  and and_58 (and_58_out, not_394_out, not_395_out, not_396_out, not_397_out, not_398_out, not_399_out, not_400_out, not_401_out, not_402_out, F2, F1, not_403_out);
  and and_59 (and_59_out, not_404_out, not_405_out, not_406_out, not_407_out, not_408_out, not_409_out, not_410_out, not_411_out, not_412_out, F2, F1, F0);
  and and_60 (BEQ, not_413_out, not_414_out, not_415_out, OP2, not_416_out, not_417_out);
  and and_61 (BNE, not_418_out, not_419_out, not_420_out, OP2, not_421_out, OP0);
  and and_62 (JR, not_422_out, not_423_out, not_424_out, not_425_out, not_426_out, not_427_out, not_428_out, not_429_out, F3, not_430_out, not_431_out, not_432_out);
  and and_63 (JMP, not_433_out, not_434_out, not_435_out, not_436_out, OP1, not_437_out);
  and and_64 (JAL, not_438_out, not_439_out, not_440_out, not_441_out, OP1, OP0);
  or or_1 (ALU_SRC, and_3_out, and_4_out, and_5_out, and_6_out, and_7_out, and_8_out, and_9_out, and_10_out, and_11_out);
  or or_2 (SignedExt, and_38_out, and_39_out, and_40_out, and_41_out, and_42_out, and_43_out);
  or or_3 (RegWrite, and_12_out, and_13_out, and_14_out, and_15_out, and_16_out, and_17_out, and_18_out, and_19_out, and_20_out, and_21_out, and_22_out, and_23_out, and_24_out, and_25_out, and_26_out, and_27_out, and_28_out, and_29_out, and_30_out, and_31_out, and_32_out, and_33_out, and_34_out, and_35_out, and_36_out);
  or or_4 (RegDst, and_44_out, and_45_out, and_46_out, and_47_out, and_48_out, and_49_out, and_50_out, and_51_out, and_52_out, and_53_out, and_54_out, and_55_out, and_56_out, and_57_out, and_58_out, and_59_out);
endmodule

module \控制信号生成2  (
  input  OP0,
  input  OP1,
  input  OP2,
  input  OP3,
  input  OP4,
  input  OP5,
  input  F0,
  input  F1,
  input  F2,
  input  F3,
  input  F4,
  input  F5,
  output ShiftVar
);

  wire and_1_out, and_2_out, and_3_out, not_1_out, not_2_out, not_3_out, not_4_out, not_5_out, not_6_out,
       not_7_out, not_8_out, not_9_out, not_10_out, not_11_out, not_12_out, not_13_out, not_14_out,
       not_15_out, not_16_out, not_17_out, not_18_out, not_19_out, not_20_out, not_21_out, not_22_out,
       not_23_out, not_24_out, not_25_out, not_26_out, not_27_out, not_28_out, not_29_out, not_30_out;

  not not_1 (not_1_out, OP5);
  not not_2 (not_2_out, OP4);
  not not_3 (not_3_out, OP3);
  not not_4 (not_4_out, OP2);
  not not_5 (not_5_out, OP1);
  not not_6 (not_6_out, OP0);
  not not_7 (not_7_out, F5);
  not not_8 (not_8_out, F4);
  not not_9 (not_9_out, F3);
  not not_10 (not_10_out, F1);
  not not_11 (not_11_out, F0);
  not not_12 (not_12_out, OP5);
  not not_13 (not_13_out, OP4);
  not not_14 (not_14_out, OP3);
  not not_15 (not_15_out, OP2);
  not not_16 (not_16_out, OP1);
  not not_17 (not_17_out, OP0);
  not not_18 (not_18_out, F5);
  not not_19 (not_19_out, F4);
  not not_20 (not_20_out, F3);
  not not_21 (not_21_out, F0);
  not not_22 (not_22_out, OP5);
  not not_23 (not_23_out, OP4);
  not not_24 (not_24_out, OP3);
  not not_25 (not_25_out, OP2);
  not not_26 (not_26_out, OP1);
  not not_27 (not_27_out, OP0);
  not not_28 (not_28_out, F5);
  not not_29 (not_29_out, F4);
  not not_30 (not_30_out, F3);
  and and_1 (and_1_out, not_1_out, not_2_out, not_3_out, not_4_out, not_5_out, not_6_out, not_7_out, not_8_out, not_9_out, F2, not_10_out, not_11_out);
  and and_2 (and_2_out, not_12_out, not_13_out, not_14_out, not_15_out, not_16_out, not_17_out, not_18_out, not_19_out, not_20_out, F2, F1, not_21_out);
  and and_3 (and_3_out, not_22_out, not_23_out, not_24_out, not_25_out, not_26_out, not_27_out, not_28_out, not_29_out, not_30_out, F2, F1, F0);
  or or_1 (ShiftVar, and_1_out, and_2_out, and_3_out);
endmodule

module ALU (
  input  [4:0] shamt,
  input  [31:0] X,
  input  [31:0] Y,
  input  [3:0] AluOP,
  output Equal,
  output [31:0] Result,
  output [31:0] Result_2
);

  wire [0:0] comparator_1_lt, comparator_2_lt;
  wire [31:0] adder_1_out, AND_out, divider_1_out, divider_1_rem, multiplier_1_cout, multiplier_1_out,
       NOR_out, OR_out, shifter_1_out, shifter_2_out, shifter_3_out, subtractor_1_out, XOR_out;

  assign AND_out = X & Y;  // AND_Gate AND, 32 bits wide
  assign OR_out = X | Y;  // OR_Gate OR, 32 bits wide
  Shifter #(.width(32), .shift("ll")) shifter_1 (.in(Y), .\dist (shamt), .out(shifter_1_out));
  Shifter #(.width(32), .shift("ar")) shifter_2 (.in(Y), .\dist (shamt), .out(shifter_2_out));
  Shifter #(.width(32), .shift("lr")) shifter_3 (.in(Y), .\dist (shamt), .out(shifter_3_out));
  Multiplier #(.width(32)) multiplier_1 (.a(X), .b(Y), .out(multiplier_1_out), .cout(multiplier_1_cout));  // open: cin
  Divider #(.width(32)) divider_1 (.a(X), .b(Y), .out(divider_1_out), .rem(divider_1_rem));  // open: upper
  Adder #(.width(32)) adder_1 (.a(X), .b(Y), .out(adder_1_out));  // open: cin, cout
  Subtractor #(.width(32)) subtractor_1 (.a(X), .b(Y), .out(subtractor_1_out));  // open: bin, bout
  assign XOR_out = X ^ Y;  // XOR_Gate XOR, 32 bits wide
  assign NOR_out = ~(X | Y);  // NOR_Gate NOR, 32 bits wide
  Comparator #(.width(32), .mode("twosComplement")) comparator_1 (
    .a(X), .b(Y), .eq(Equal), .lt(comparator_1_lt[0]));  // open: gt
  Comparator #(.width(32), .mode("unsigned")) comparator_2 (.a(X), .b(Y), .lt(comparator_2_lt[0]));  // open: gt, eq
  Multiplexer #(.select(4), .width(32), .disabled("Z"), .enable("false")) multiplexer_1 (
    .in0(shifter_1_out), .in1(shifter_2_out), .in2(shifter_3_out), .in3(multiplier_1_out),
    .in4(divider_1_out), .in5(adder_1_out), .in6(subtractor_1_out), .in7(AND_out), .in8(OR_out),
    .in9(XOR_out), .in10(NOR_out), .in11({{31{1'b0}}, comparator_1_lt[0]}),
    .in12({{31{1'b0}}, comparator_2_lt[0]}), .in13({32{1'b0}}), .in14({32{1'b0}}), .in15({32{1'b0}}),
    .out(Result), .sel(AluOP));
  Multiplexer #(.select(4), .width(32), .disabled("Z"), .enable("false")) multiplexer_2 (
    .in0({32{1'b0}}), .in1({32{1'b0}}), .in2({32{1'b0}}), .in3(multiplier_1_cout), .in4(divider_1_rem),
    .in5({32{1'b0}}), .in6({32{1'b0}}), .in7({32{1'b0}}), .in8({32{1'b0}}), .in9({32{1'b0}}),
    .in10({32{1'b0}}), .in11({32{1'b0}}), .in12({32{1'b0}}), .in13({32{1'b0}}), .in14({32{1'b0}}),
    .in15({32{1'b0}}), .out(Result_2), .sel(AluOP));

  // Other names for the same wires on the sheet: Result2[31:0] = Result_2; S[3:0] = AluOP

  // Notes on the sheet:
  //   输入引脚
  //   输出引脚
endmodule

module Regifile (
  input  [31:0] Din,
  input  Clk,
  input  WE,
  input  [4:0] R1_num,
  input  [4:0] W_num,
  input  [4:0] R2_num,
  output [31:0] R1,
  output [31:0] R2
);

  // RegisterFile registerfile_1: pin names not known; wires that end beside it: Din, Clk, WE, W_num, R1_num, R2_num, R1, R2
endmodule

module \寄存器文件  (
  input  [4:0] in_1,
  input  in_2,
  input  [31:0] in_3,
  input  [4:0] in_4,
  input  in_5,
  input  [4:0] in_6,
  output [31:0] out_7,
  output [31:0] out_8
);

  wire EN0, EN1, EN2, EN3, EN4, EN5, EN6, EN7, EN8, EN9, EN10, EN11, EN12, EN13, EN14, EN15, EN16, EN17,
       EN18, EN19, EN20, EN21, EN22, EN23, EN24, EN25, EN26, EN27, EN28, EN29, EN30, EN31;
  wire [4:0] multiplexer_1_out;
  wire [31:0] _0_q, _1_q, _2_q, _3_q, _4_q, _5_q, _6_q, _7_q, _8_q, _9_q, _10_q, _11_q, _12_q, _13_q, _14_q,
       _15_q, _16_q, _17_q, _18_q, _19_q, _20_q, _21_q, _22_q, _23_q, _24_q, _25_q, _26_q, _27_q, _28_q,
       _29_q, _30_q, _31_q;

  Decoder #(.select(5), .tristate("false"), .disabled("Z"), .enable("false")) decoder_1 (
    .out0(EN0), .out1(EN1), .out2(EN2), .out3(EN3), .out4(EN4), .out5(EN5), .out6(EN6), .out7(EN7),
    .out8(EN8), .out9(EN9), .out10(EN10), .out11(EN11), .out12(EN12), .out13(EN13), .out14(EN14),
    .out15(EN15), .out16(EN16), .out17(EN17), .out18(EN18), .out19(EN19), .out20(EN20), .out21(EN21),
    .out22(EN22), .out23(EN23), .out24(EN24), .out25(EN25), .out26(EN26), .out27(EN27), .out28(EN28),
    .out29(EN29), .out30(EN30), .out31(EN31), .sel(multiplexer_1_out));
  Multiplexer #(.select(1), .width(5), .disabled("Z"), .enable("false")) multiplexer_1 (
    .in0({5{1'b0}}), .in1(in_6), .out(multiplexer_1_out), .sel(in_2));
  Register #(.width(32), .trigger("rising"), .Select("low")) _0 (
    .D({32{1'b0}}), .en(EN0), .Q(_0_q), .clk(in_5));  // open: clr
  Register #(.width(32), .trigger("rising"), .Select("low")) _8 (
    .D(in_3), .en(EN8), .Q(_8_q), .clk(in_5));  // open: clr
  Register #(.width(32), .trigger("rising"), .Select("low")) _16 (
    .D(in_3), .en(EN16), .Q(_16_q), .clk(in_5));  // open: clr
  Register #(.width(32), .trigger("rising"), .Select("low")) _24 (
    .D(in_3), .en(EN24), .Q(_24_q), .clk(in_5));  // open: clr
  Register #(.width(32), .trigger("rising"), .Select("low")) _1 (
    .D(in_3), .en(EN1), .Q(_1_q), .clk(in_5));  // open: clr
  Register #(.width(32), .trigger("rising"), .Select("low")) _9 (
    .D(in_3), .en(EN9), .Q(_9_q), .clk(in_5));  // open: clr
  Register #(.width(32), .trigger("rising"), .Select("low")) _17 (
    .D(in_3), .en(EN17), .Q(_17_q), .clk(in_5));  // open: clr
  Register #(.width(32), .trigger("rising"), .Select("low")) _25 (
    .D(in_3), .en(EN25), .Q(_25_q), .clk(in_5));  // open: clr
  Register #(.width(32), .trigger("rising"), .Select("low")) _2 (
    .D(in_3), .en(EN2), .Q(_2_q), .clk(in_5));  // open: clr
  Register #(.width(32), .trigger("rising"), .Select("low")) _10 (
    .D(in_3), .en(EN10), .Q(_10_q), .clk(in_5));  // open: clr
  Register #(.width(32), .trigger("rising"), .Select("low")) _18 (
    .D(in_3), .en(EN18), .Q(_18_q), .clk(in_5));  // open: clr
  Register #(.width(32), .trigger("rising"), .Select("low")) _26 (
    .D(in_3), .en(EN26), .Q(_26_q), .clk(in_5));  // open: clr
  Register #(.width(32), .trigger("rising"), .Select("low")) _3 (
    .D(in_3), .en(EN3), .Q(_3_q), .clk(in_5));  // open: clr
  Register #(.width(32), .trigger("rising"), .Select("low")) _11 (
    .D(in_3), .en(EN11), .Q(_11_q), .clk(in_5));  // open: clr
  Register #(.width(32), .trigger("rising"), .Select("low")) _19 (
    .D(in_3), .en(EN19), .Q(_19_q), .clk(in_5));  // open: clr
  Register #(.width(32), .trigger("rising"), .Select("low")) _27 (
    .D(in_3), .en(EN27), .Q(_27_q), .clk(in_5));  // open: clr
  Register #(.width(32), .trigger("rising"), .Select("low")) _4 (
    .D(in_3), .en(EN4), .Q(_4_q), .clk(in_5));  // open: clr
  Register #(.width(32), .trigger("rising"), .Select("low")) _12 (
    .D(in_3), .en(EN12), .Q(_12_q), .clk(in_5));  // open: clr
  Register #(.width(32), .trigger("rising"), .Select("low")) _20 (
    .D(in_3), .en(EN20), .Q(_20_q), .clk(in_5));  // open: clr
  Register #(.width(32), .trigger("rising"), .Select("low")) _28 (
    .D(in_3), .en(EN28), .Q(_28_q), .clk(in_5));  // open: clr
  Register #(.width(32), .trigger("rising"), .Select("low")) _5 (
    .D(in_3), .en(EN5), .Q(_5_q), .clk(in_5));  // open: clr
  Register #(.width(32), .trigger("rising"), .Select("low")) _13 (
    .D(in_3), .en(EN13), .Q(_13_q), .clk(in_5));  // open: clr
  Register #(.width(32), .trigger("rising"), .Select("low")) _21 (
    .D(in_3), .en(EN21), .Q(_21_q), .clk(in_5));  // open: clr
  Register #(.width(32), .trigger("rising"), .Select("low")) _29 (
    .D(in_3), .en(EN29), .Q(_29_q), .clk(in_5));  // open: clr
  Register #(.width(32), .trigger("rising"), .Select("low")) _6 (
    .D(in_3), .en(EN6), .Q(_6_q), .clk(in_5));  // open: clr
  Register #(.width(32), .trigger("rising"), .Select("low")) _14 (
    .D(in_3), .en(EN14), .Q(_14_q), .clk(in_5));  // open: clr
  Register #(.width(32), .trigger("rising"), .Select("low")) _22 (
    .D(in_3), .en(EN22), .Q(_22_q), .clk(in_5));  // open: clr
  Register #(.width(32), .trigger("rising"), .Select("low")) _30 (
    .D(in_3), .en(EN30), .Q(_30_q), .clk(in_5));  // open: clr
  Register #(.width(32), .trigger("rising"), .Select("low")) _7 (
    .D(in_3), .en(EN7), .Q(_7_q), .clk(in_5));  // open: clr
  Register #(.width(32), .trigger("rising"), .Select("low")) _15 (
    .D(in_3), .en(EN15), .Q(_15_q), .clk(in_5));  // open: clr
  Register #(.width(32), .trigger("rising"), .Select("low")) _23 (
    .D(in_3), .en(EN23), .Q(_23_q), .clk(in_5));  // open: clr
  Register #(.width(32), .trigger("rising"), .Select("low")) _31 (
    .D(in_3), .en(EN31), .Q(_31_q), .clk(in_5));  // open: clr
  Multiplexer #(.select(5), .width(32), .disabled("Z"), .enable("false")) multiplexer_2 (
    .in0(_0_q), .in1(_1_q), .in2(_2_q), .in3(_3_q), .in4(_4_q), .in5(_5_q), .in6(_6_q), .in7(_7_q),
    .in8(_8_q), .in9(_9_q), .in10(_10_q), .in11(_11_q), .in12(_12_q), .in13(_13_q), .in14(_14_q),
    .in15(_15_q), .in16(_16_q), .in17(_17_q), .in18(_18_q), .in19(_19_q), .in20(_20_q), .in21(_21_q),
    .in22(_22_q), .in23(_23_q), .in24(_24_q), .in25(_25_q), .in26(_26_q), .in27(_27_q), .in28(_28_q),
    .in29(_29_q), .in30(_30_q), .in31(_31_q), .out(out_7), .sel(in_1));
  Multiplexer #(.select(5), .width(32), .disabled("Z"), .enable("false")) multiplexer_3 (
    .in0(_0_q), .in1(_1_q), .in2(_2_q), .in3(_3_q), .in4(_4_q), .in5(_5_q), .in6(_6_q), .in7(_7_q),
    .in8(_8_q), .in9(_9_q), .in10(_10_q), .in11(_11_q), .in12(_12_q), .in13(_13_q), .in14(_14_q),
    .in15(_15_q), .in16(_16_q), .in17(_17_q), .in18(_18_q), .in19(_19_q), .in20(_20_q), .in21(_21_q),
    .in22(_22_q), .in23(_23_q), .in24(_24_q), .in25(_25_q), .in26(_26_q), .in27(_27_q), .in28(_28_q),
    .in29(_29_q), .in30(_30_q), .in31(_31_q), .out(out_8), .sel(in_4));

  // Other names for the same wires on the sheet: CLK = in_5; Din[31:0] = in_3; R1[31:0] = out_7; R1_num[4:0] = in_1;
  //   R2[31:0] = out_8; R2_num[4:0] = in_4; W_num[4:0] = in_6; WE = in_2
endmodule

module \符号扩展  (
  input  [15:0] in_1,
  input  in_2,
  output [31:0] out_3
);

  wire [31:0] bit_extender_1_out, bit_extender_2_out;

  assign bit_extender_1_out = {{16{1'b0}}, in_1};  // Bit_Extender bit_extender_1
  assign bit_extender_2_out = {{16{in_1[15]}}, in_1};  // Bit_Extender bit_extender_2
  Multiplexer #(.select(1), .width(32), .disabled("Z"), .enable("true")) multiplexer_1 (
    .in0(bit_extender_1_out), .in1(bit_extender_2_out), .out(out_3), .sel(in_2));  // open: en
endmodule

module IF_ID (
  input  [31:0] instruction,
  input  EN,
  input  CLK,
  input  \Clear_同步清零 ,
  input  [31:0] PC,
  output [31:0] IR,
  output [5:0] OP,
  output [5:0] Func,
  output [4:0] Rs,
  output [4:0] Rt,
  output [4:0] Rd,
  output [15:0] Imm,
  output [4:0] Shamt,
  output [25:0] Address,
  output [4:0] Rt_2,
  output [31:0] PC_2
);

  wire [31:0] multiplexer_1_out, multiplexer_2_out;

  Multiplexer #(.select(1), .width(32), .disabled("Z"), .enable("true")) multiplexer_1 (
    .in0(instruction), .in1({32{1'b0}}), .out(multiplexer_1_out), .sel(\Clear_同步清零 ));  // open: en
  Pull_Resistor #(.pull(0)) pull_resistor_1 (.node(\Clear_同步清零 ));
  Multiplexer #(.select(1), .width(32), .disabled("Z"), .enable("true")) multiplexer_2 (
    .in0(PC), .in1({32{1'b0}}), .out(multiplexer_2_out), .sel(\Clear_同步清零 ));  // open: en
  Register #(.width(32), .trigger("rising"), .Select("low")) register_1 (
    .D(multiplexer_1_out), .en(EN), .Q({IR[31:26], Address}), .clk(CLK));  // open: clr
  Register #(.width(32), .trigger("rising"), .Select("low")) register_2 (
    .D(multiplexer_2_out), .en(EN), .Q(PC_2), .clk(CLK));  // open: clr

  assign Func = Address[5:0];
  assign Imm = Address[15:0];
  assign IR[25:0] = Address;
  assign OP = IR[31:26];
  assign Rd = Address[15:11];
  assign Rs = Address[25:21];
  assign Rt = Address[20:16];
  assign Rt_2 = Address[20:16];
  assign Shamt = Address[10:6];

  // Notes on the sheet:
  //   OP
  //   Func
  //   rs
  //   rt
  //   rd
  //   Imm
  //   shamt
  //   address
  //   rt
endmodule
module ID_EX (
  input  in_1,
  input  in_2,
  input  in_3,
  input  in_4,
  input  in_5,
  input  in_6,
  input  in_7,
  input  in_8,
  input  in_9,
  input  in_10,
  input  in_11,
  input  in_12,
  input  in_13,
  input  [3:0] in_14,
  input  in_15,
  input  [31:0] R1,
  input  [1:0] AUL_Src1,
  input  [31:0] R2,
  input  [1:0] R2EXMEM,
  input  [31:0] Imm,
  input  [4:0] Shamt,
  input  [25:0] Address,
  input  [31:0] PC,
  input  [4:0] Rt,
  input  [4:0] Rd,
  input  [31:0] IR,
  input  EN,
  input  \Clear_同步清零高电平有效 ,
  input  CLK,
  output out_30,
  output out_31,
  output out_32,
  output out_33,
  output out_34,
  output out_35,
  output out_36,
  output out_37,
  output out_38,
  output out_39,
  output out_40,
  output out_41,
  output out_42,
  output [3:0] out_43,
  output out_44,
  output [31:0] R1_2,
  output [1:0] ALU_Src1,
  output [31:0] R2_2,
  output [1:0] R2EXMEM_2,
  output [31:0] Imm_2,
  output [4:0] Shamt_2,
  output [25:0] Address_2,
  output [31:0] PC_2,
  output [4:0] Rt_2,
  output [4:0] Rd_2,
  output [31:0] IR_2
);

  wire multiplexer_1_out, multiplexer_2_out, multiplexer_3_out, multiplexer_4_out, multiplexer_5_out,
       multiplexer_6_out, multiplexer_7_out, multiplexer_8_out, multiplexer_9_out, multiplexer_10_out,
       multiplexer_11_out, multiplexer_12_out, multiplexer_13_out, multiplexer_15_out;
  wire [1:0] multiplexer_17_out, multiplexer_19_out;
  wire [3:0] multiplexer_14_out;
  wire [4:0] multiplexer_21_out, multiplexer_24_out, multiplexer_25_out;
  wire [25:0] multiplexer_22_out;
  wire [31:0] multiplexer_16_out, multiplexer_18_out, multiplexer_20_out, multiplexer_23_out,
       multiplexer_26_out;

  Pull_Resistor #(.pull(0)) pull_resistor_1 (.node(\Clear_同步清零高电平有效 ));
  Multiplexer #(.select(1), .width(1), .disabled("Z"), .enable("true")) multiplexer_1 (
    .in0(in_1), .in1(1'b0), .out(multiplexer_1_out), .sel(\Clear_同步清零高电平有效 ));  // open: en
  Multiplexer #(.select(1), .width(1), .disabled("Z"), .enable("true")) multiplexer_2 (
    .in0(in_2), .in1(1'b0), .out(multiplexer_2_out), .sel(\Clear_同步清零高电平有效 ));  // open: en
  Multiplexer #(.select(1), .width(1), .disabled("Z"), .enable("true")) multiplexer_3 (
    .in0(in_3), .in1(1'b0), .out(multiplexer_3_out), .sel(\Clear_同步清零高电平有效 ));  // open: en
  Multiplexer #(.select(1), .width(1), .disabled("Z"), .enable("true")) multiplexer_4 (
    .in0(in_4), .in1(1'b0), .out(multiplexer_4_out), .sel(\Clear_同步清零高电平有效 ));  // open: en
  Multiplexer #(.select(1), .width(1), .disabled("Z"), .enable("true")) multiplexer_5 (
    .in0(in_5), .in1(1'b0), .out(multiplexer_5_out), .sel(\Clear_同步清零高电平有效 ));  // open: en
  Multiplexer #(.select(1), .width(1), .disabled("Z"), .enable("true")) multiplexer_6 (
    .in0(in_6), .in1(1'b0), .out(multiplexer_6_out), .sel(\Clear_同步清零高电平有效 ));  // open: en
  Multiplexer #(.select(1), .width(1), .disabled("Z"), .enable("true")) multiplexer_7 (
    .in0(in_7), .in1(1'b0), .out(multiplexer_7_out), .sel(\Clear_同步清零高电平有效 ));  // open: en
  Multiplexer #(.select(1), .width(1), .disabled("Z"), .enable("true")) multiplexer_8 (
    .in0(in_8), .in1(1'b0), .out(multiplexer_8_out), .sel(\Clear_同步清零高电平有效 ));  // open: en
  Multiplexer #(.select(1), .width(1), .disabled("Z"), .enable("true")) multiplexer_9 (
    .in0(in_9), .in1(1'b0), .out(multiplexer_9_out), .sel(\Clear_同步清零高电平有效 ));  // open: en
  Multiplexer #(.select(1), .width(1), .disabled("Z"), .enable("true")) multiplexer_10 (
    .in0(in_10), .in1(1'b0), .out(multiplexer_10_out), .sel(\Clear_同步清零高电平有效 ));  // open: en
  Multiplexer #(.select(1), .width(1), .disabled("Z"), .enable("true")) multiplexer_11 (
    .in0(in_11), .in1(1'b0), .out(multiplexer_11_out), .sel(\Clear_同步清零高电平有效 ));  // open: en
  Multiplexer #(.select(1), .width(1), .disabled("Z"), .enable("true")) multiplexer_12 (
    .in0(in_12), .in1(1'b0), .out(multiplexer_12_out), .sel(\Clear_同步清零高电平有效 ));  // open: en
  Multiplexer #(.select(1), .width(1), .disabled("Z"), .enable("true")) multiplexer_13 (
    .in0(in_13), .in1(1'b0), .out(multiplexer_13_out), .sel(\Clear_同步清零高电平有效 ));  // open: en
  Multiplexer #(.select(1), .width(4), .disabled("Z"), .enable("true")) multiplexer_14 (
    .in0(in_14), .in1(4'b0000), .out(multiplexer_14_out), .sel(\Clear_同步清零高电平有效 ));  // open: en
  Multiplexer #(.select(1), .width(1), .disabled("Z"), .enable("true")) multiplexer_15 (
    .in0(in_15), .in1(1'b0), .out(multiplexer_15_out), .sel(\Clear_同步清零高电平有效 ));  // open: en
  Multiplexer #(.select(1), .width(32), .disabled("Z"), .enable("true")) multiplexer_16 (
    .in0(R1), .in1({32{1'b0}}), .out(multiplexer_16_out), .sel(\Clear_同步清零高电平有效 ));  // open: en
  Multiplexer #(.select(1), .width(2), .disabled("Z"), .enable("true")) multiplexer_17 (
    .in0(AUL_Src1), .in1(2'b00), .out(multiplexer_17_out), .sel(\Clear_同步清零高电平有效 ));  // open: en
  Multiplexer #(.select(1), .width(32), .disabled("Z"), .enable("true")) multiplexer_18 (
    .in0(R2), .in1({32{1'b0}}), .out(multiplexer_18_out), .sel(\Clear_同步清零高电平有效 ));  // open: en
  Multiplexer #(.select(1), .width(2), .disabled("Z"), .enable("true")) multiplexer_19 (
    .in0(R2EXMEM), .in1(2'b00), .out(multiplexer_19_out), .sel(\Clear_同步清零高电平有效 ));  // open: en
  Multiplexer #(.select(1), .width(32), .disabled("Z"), .enable("true")) multiplexer_20 (
    .in0(Imm), .in1({32{1'b0}}), .out(multiplexer_20_out), .sel(\Clear_同步清零高电平有效 ));  // open: en
  Multiplexer #(.select(1), .width(5), .disabled("Z"), .enable("true")) multiplexer_21 (
    .in0(Shamt), .in1({5{1'b0}}), .out(multiplexer_21_out), .sel(\Clear_同步清零高电平有效 ));  // open: en
  Multiplexer #(.select(1), .width(26), .disabled("Z"), .enable("true")) multiplexer_22 (
    .in0(Address), .in1({26{1'b0}}), .out(multiplexer_22_out), .sel(\Clear_同步清零高电平有效 ));  // open: en
  Multiplexer #(.select(1), .width(32), .disabled("Z"), .enable("true")) multiplexer_23 (
    .in0(PC), .in1({32{1'b0}}), .out(multiplexer_23_out), .sel(\Clear_同步清零高电平有效 ));  // open: en
  Multiplexer #(.select(1), .width(5), .disabled("Z"), .enable("true")) multiplexer_24 (
    .in0(Rt), .in1({5{1'b0}}), .out(multiplexer_24_out), .sel(\Clear_同步清零高电平有效 ));  // open: en
  Multiplexer #(.select(1), .width(5), .disabled("Z"), .enable("true")) multiplexer_25 (
    .in0(Rd), .in1({5{1'b0}}), .out(multiplexer_25_out), .sel(\Clear_同步清零高电平有效 ));  // open: en
  Multiplexer #(.select(1), .width(32), .disabled("Z"), .enable("true")) multiplexer_26 (
    .in0(IR), .in1({32{1'b0}}), .out(multiplexer_26_out), .sel(\Clear_同步清零高电平有效 ));  // open: en
  Register #(.width(1), .trigger("rising"), .Select("low")) register_1 (
    .D(multiplexer_1_out), .en(EN), .Q(out_30), .clk(CLK));  // open: clr
  Register #(.width(1), .trigger("rising"), .Select("low")) register_2 (
    .D(multiplexer_2_out), .en(EN), .Q(out_31), .clk(CLK));  // open: clr
  Register #(.width(1), .trigger("rising"), .Select("low")) register_3 (
    .D(multiplexer_3_out), .en(EN), .Q(out_32), .clk(CLK));  // open: clr
  Register #(.width(1), .trigger("rising"), .Select("low")) register_4 (
    .D(multiplexer_4_out), .en(EN), .Q(out_33), .clk(CLK));  // open: clr
  Register #(.width(1), .trigger("rising"), .Select("low")) register_5 (
    .D(multiplexer_5_out), .en(EN), .Q(out_34), .clk(CLK));  // open: clr
  Register #(.width(1), .trigger("rising"), .Select("low")) register_6 (
    .D(multiplexer_6_out), .en(EN), .Q(out_35), .clk(CLK));  // open: clr
  Register #(.width(1), .trigger("rising"), .Select("low")) register_7 (
    .D(multiplexer_7_out), .en(EN), .Q(out_36), .clk(CLK));  // open: clr
  Register #(.width(1), .trigger("rising"), .Select("low")) register_8 (
    .D(multiplexer_8_out), .en(EN), .Q(out_37), .clk(CLK));  // open: clr
  Register #(.width(1), .trigger("rising"), .Select("low")) register_9 (
    .D(multiplexer_9_out), .en(EN), .Q(out_38), .clk(CLK));  // open: clr
  Register #(.width(1), .trigger("rising"), .Select("low")) register_10 (
    .D(multiplexer_10_out), .en(EN), .Q(out_39), .clk(CLK));  // open: clr
  Register #(.width(1), .trigger("rising"), .Select("low")) register_11 (
    .D(multiplexer_11_out), .en(EN), .Q(out_40), .clk(CLK));  // open: clr
  Register #(.width(1), .trigger("rising"), .Select("low")) register_12 (
    .D(multiplexer_12_out), .en(EN), .Q(out_41), .clk(CLK));  // open: clr
  Register #(.width(1), .trigger("rising"), .Select("low")) register_13 (
    .D(multiplexer_13_out), .en(EN), .Q(out_42), .clk(CLK));  // open: clr
  Register #(.width(4), .trigger("rising"), .Select("low")) register_14 (
    .D(multiplexer_14_out), .en(EN), .Q(out_43), .clk(CLK));  // open: clr
  Register #(.width(1), .trigger("rising"), .Select("low")) register_15 (
    .D(multiplexer_15_out), .en(EN), .Q(out_44), .clk(CLK));  // open: clr
  Register #(.width(32), .trigger("rising"), .Select("low")) register_16 (
    .D(multiplexer_16_out), .en(EN), .Q(R1_2), .clk(CLK));  // open: clr
  Register #(.width(2), .trigger("rising"), .Select("low")) register_17 (
    .D(multiplexer_17_out), .en(EN), .Q(ALU_Src1), .clk(CLK));  // open: clr
  Register #(.width(32), .trigger("rising"), .Select("low")) register_18 (
    .D(multiplexer_18_out), .en(EN), .Q(R2_2), .clk(CLK));  // open: clr
  Register #(.width(2), .trigger("rising"), .Select("low")) register_19 (
    .D(multiplexer_19_out), .en(EN), .Q(R2EXMEM_2), .clk(CLK));  // open: clr
  Register #(.width(32), .trigger("rising"), .Select("low")) register_20 (
    .D(multiplexer_20_out), .en(EN), .Q(Imm_2), .clk(CLK));  // open: clr
  Register #(.width(5), .trigger("rising"), .Select("low")) register_21 (
    .D(multiplexer_21_out), .en(EN), .Q(Shamt_2), .clk(CLK));  // open: clr
  Register #(.width(26), .trigger("rising"), .Select("low")) register_22 (
    .D(multiplexer_22_out), .en(EN), .Q(Address_2), .clk(CLK));  // open: clr
  Register #(.width(32), .trigger("rising"), .Select("low")) register_23 (
    .D(multiplexer_23_out), .en(EN), .Q(PC_2), .clk(CLK));  // open: clr
  Register #(.width(5), .trigger("rising"), .Select("low")) register_24 (
    .D(multiplexer_24_out), .en(EN), .Q(Rt_2), .clk(CLK));  // open: clr
  Register #(.width(5), .trigger("rising"), .Select("low")) register_25 (
    .D(multiplexer_25_out), .en(EN), .Q(Rd_2), .clk(CLK));  // open: clr
  Register #(.width(32), .trigger("rising"), .Select("low")) register_26 (
    .D(multiplexer_26_out), .en(EN), .Q(IR_2), .clk(CLK));  // open: clr
endmodule

module EX_MEM (
  input  in_1,
  input  in_2,
  input  in_3,
  input  in_4,
  input  in_5,
  input  [31:0] R1,
  input  [31:0] R2,
  input  in_8,
  input  [31:0] ALU_Result,
  input  [31:0] PC,
  input  [4:0] Rt,
  input  [4:0] Rd,
  input  [31:0] IR,
  input  EN,
  input  CLK,
  input  Clear,
  output out_17,
  output out_18,
  output out_19,
  output out_20,
  output out_21,
  output [31:0] R1_2,
  output [31:0] R2_2,
  output out_24,
  output [31:0] ALU_Result_2,
  output [31:0] PC_2,
  output [4:0] Rt_2,
  output [4:0] Rd_2,
  output [31:0] IR_2
);

  wire multiplexer_1_out, multiplexer_2_out, multiplexer_3_out, multiplexer_4_out, multiplexer_5_out,
       multiplexer_8_out;
  wire [4:0] multiplexer_10_out, multiplexer_11_out;
  wire [31:0] multiplexer_6_out, multiplexer_7_out, multiplexer_9_out, multiplexer_12_out;

  Pull_Resistor #(.pull(0)) pull_resistor_1 (.node(Clear));
  Multiplexer #(.select(1), .width(1), .disabled("Z"), .enable("true")) multiplexer_1 (
    .in0(in_1), .in1(1'b0), .out(multiplexer_1_out), .sel(Clear));  // open: en
  Multiplexer #(.select(1), .width(1), .disabled("Z"), .enable("true")) multiplexer_2 (
    .in0(in_2), .in1(1'b0), .out(multiplexer_2_out), .sel(Clear));  // open: en
  Multiplexer #(.select(1), .width(1), .disabled("Z"), .enable("true")) multiplexer_3 (
    .in0(in_3), .in1(1'b0), .out(multiplexer_3_out), .sel(Clear));  // open: en
  Multiplexer #(.select(1), .width(1), .disabled("Z"), .enable("true")) multiplexer_4 (
    .in0(in_4), .in1(1'b0), .out(multiplexer_4_out), .sel(Clear));  // open: en
  Multiplexer #(.select(1), .width(1), .disabled("Z"), .enable("true")) multiplexer_5 (
    .in0(in_5), .in1(1'b0), .out(multiplexer_5_out), .sel(Clear));  // open: en
  Multiplexer #(.select(1), .width(32), .disabled("Z"), .enable("true")) multiplexer_6 (
    .in0(R1), .in1({32{1'b0}}), .out(multiplexer_6_out), .sel(Clear));  // open: en
  Multiplexer #(.select(1), .width(32), .disabled("Z"), .enable("true")) multiplexer_7 (
    .in0(R2), .in1({32{1'b0}}), .out(multiplexer_7_out), .sel(Clear));  // open: en
  Multiplexer #(.select(1), .width(1), .disabled("Z"), .enable("true")) multiplexer_8 (
    .in0(in_8), .in1(1'b0), .out(multiplexer_8_out), .sel(Clear));  // open: en
  Multiplexer #(.select(1), .width(32), .disabled("Z"), .enable("true")) multiplexer_9 (
    .in0(ALU_Result), .in1({32{1'b0}}), .out(multiplexer_9_out), .sel(Clear));  // open: en
  Multiplexer #(.select(1), .width(5), .disabled("Z"), .enable("true")) multiplexer_10 (
    .in0(Rt), .in1({5{1'b0}}), .out(multiplexer_10_out), .sel(Clear));  // open: en
  Multiplexer #(.select(1), .width(5), .disabled("Z"), .enable("true")) multiplexer_11 (
    .in0(Rd), .in1({5{1'b0}}), .out(multiplexer_11_out), .sel(Clear));  // open: en
  Multiplexer #(.select(1), .width(32), .disabled("Z"), .enable("true")) multiplexer_12 (
    .in0(IR), .in1({32{1'b0}}), .out(multiplexer_12_out), .sel(Clear));  // open: en
  Register #(.width(1), .trigger("rising"), .Select("low")) register_1 (
    .D(multiplexer_1_out), .en(EN), .Q(out_17), .clk(CLK));  // open: clr
  Register #(.width(1), .trigger("rising"), .Select("low")) register_2 (
    .D(multiplexer_2_out), .en(EN), .Q(out_18), .clk(CLK));  // open: clr
  Register #(.width(1), .trigger("rising"), .Select("low")) register_3 (
    .D(multiplexer_3_out), .en(EN), .Q(out_19), .clk(CLK));  // open: clr
  Register #(.width(1), .trigger("rising"), .Select("low")) register_4 (
    .D(multiplexer_4_out), .en(EN), .Q(out_20), .clk(CLK));  // open: clr
  Register #(.width(1), .trigger("rising"), .Select("low")) register_5 (
    .D(multiplexer_5_out), .en(EN), .Q(out_21), .clk(CLK));  // open: clr
  Register #(.width(32), .trigger("rising"), .Select("low")) register_6 (
    .D(multiplexer_6_out), .en(EN), .Q(R1_2), .clk(CLK));  // open: clr
  Register #(.width(32), .trigger("rising"), .Select("low")) register_7 (
    .D(multiplexer_7_out), .Q(R2_2), .clk(CLK));  // open: en, clr
  Register #(.width(1), .trigger("rising"), .Select("low")) register_8 (
    .D(multiplexer_8_out), .en(EN), .Q(out_24), .clk(CLK));  // open: clr
  Register #(.width(32), .trigger("rising"), .Select("low")) register_9 (
    .D(multiplexer_9_out), .en(EN), .Q(ALU_Result_2), .clk(CLK));  // open: clr
  Register #(.width(32), .trigger("rising"), .Select("low")) register_10 (
    .D(PC), .en(EN), .Q(PC_2), .clk(CLK));  // open: clr
  Register #(.width(5), .trigger("rising"), .Select("low")) register_11 (
    .D(multiplexer_10_out), .en(EN), .Q(Rt_2), .clk(CLK));  // open: clr
  Register #(.width(5), .trigger("rising"), .Select("low")) register_12 (
    .D(multiplexer_11_out), .en(EN), .Q(Rd_2), .clk(CLK));  // open: clr
  Register #(.width(32), .trigger("rising"), .Select("low")) register_13 (
    .D(multiplexer_12_out), .en(EN), .Q(IR_2), .clk(CLK));  // open: clr
endmodule

module MEM_WB (
  input  in_1,
  input  in_2,
  input  in_3,
  input  in_4,
  input  in_5,
  input  [31:0] R1,
  input  [31:0] R2,
  input  [31:0] ALU_Result,
  input  [31:0] WD,
  input  [31:0] PC,
  input  [4:0] Rt,
  input  [4:0] Rd,
  input  [31:0] IR,
  input  EN,
  input  CLK,
  input  Clear,
  output out_17,
  output out_18,
  output out_19,
  output out_20,
  output out_21,
  output [31:0] R1_2,
  output [31:0] R2_2,
  output [31:0] ALU_Result_2,
  output [31:0] WD_2,
  output [31:0] PC_2,
  output [4:0] Rt_2,
  output [4:0] Rd_2,
  output [31:0] IR_2
);

  wire multiplexer_1_out, multiplexer_2_out, multiplexer_3_out, multiplexer_4_out, multiplexer_5_out;
  wire [4:0] multiplexer_11_out, multiplexer_12_out;
  wire [31:0] multiplexer_6_out, multiplexer_7_out, multiplexer_8_out, multiplexer_9_out, multiplexer_10_out,
       multiplexer_13_out;

  Multiplexer #(.select(1), .width(1), .disabled("Z"), .enable("true")) multiplexer_1 (
    .in0(in_1), .in1(1'b0), .out(multiplexer_1_out), .sel(Clear));  // open: en
  Multiplexer #(.select(1), .width(1), .disabled("Z"), .enable("true")) multiplexer_2 (
    .in0(in_2), .in1(1'b0), .out(multiplexer_2_out), .sel(Clear));  // open: en
  Multiplexer #(.select(1), .width(1), .disabled("Z"), .enable("true")) multiplexer_3 (
    .in0(in_3), .in1(1'b0), .out(multiplexer_3_out), .sel(Clear));  // open: en
  Multiplexer #(.select(1), .width(1), .disabled("Z"), .enable("true")) multiplexer_4 (
    .in0(in_4), .in1(1'b0), .out(multiplexer_4_out), .sel(Clear));  // open: en
  Multiplexer #(.select(1), .width(1), .disabled("Z"), .enable("true")) multiplexer_5 (
    .in0(in_5), .in1(1'b0), .out(multiplexer_5_out), .sel(Clear));  // open: en
  Multiplexer #(.select(1), .width(32), .disabled("Z"), .enable("true")) multiplexer_6 (
    .in0(R1), .in1({32{1'b0}}), .out(multiplexer_6_out), .sel(Clear));  // open: en
  Multiplexer #(.select(1), .width(32), .disabled("Z"), .enable("true")) multiplexer_7 (
    .in0(R2), .in1({32{1'b0}}), .out(multiplexer_7_out), .sel(Clear));  // open: en
  Multiplexer #(.select(1), .width(32), .disabled("Z"), .enable("true")) multiplexer_8 (
    .in0(ALU_Result), .in1({32{1'b0}}), .out(multiplexer_8_out), .sel(Clear));  // open: en
  Multiplexer #(.select(1), .width(32), .disabled("Z"), .enable("true")) multiplexer_9 (
    .in0(WD), .in1({32{1'b0}}), .out(multiplexer_9_out), .sel(Clear));  // open: en
  Multiplexer #(.select(1), .width(32), .disabled("Z"), .enable("true")) multiplexer_10 (
    .in0(PC), .in1({32{1'b0}}), .out(multiplexer_10_out), .sel(Clear));  // open: en
  Multiplexer #(.select(1), .width(5), .disabled("Z"), .enable("true")) multiplexer_11 (
    .in0(Rt), .in1({5{1'b0}}), .out(multiplexer_11_out), .sel(Clear));  // open: en
  Multiplexer #(.select(1), .width(5), .disabled("Z"), .enable("true")) multiplexer_12 (
    .in0(Rd), .in1({5{1'b0}}), .out(multiplexer_12_out), .sel(Clear));  // open: en
  Multiplexer #(.select(1), .width(32), .disabled("Z"), .enable("true")) multiplexer_13 (
    .in0(IR), .in1({32{1'b0}}), .out(multiplexer_13_out), .sel(Clear));  // open: en
  Register #(.width(1), .trigger("rising"), .Select("low")) register_1 (
    .D(multiplexer_1_out), .en(EN), .Q(out_17), .clk(CLK));  // open: clr
  Register #(.width(1), .trigger("rising"), .Select("low")) register_2 (
    .D(multiplexer_2_out), .en(EN), .Q(out_18), .clk(CLK));  // open: clr
  Register #(.width(1), .trigger("rising"), .Select("low")) register_3 (
    .D(multiplexer_3_out), .en(EN), .Q(out_19), .clk(CLK));  // open: clr
  Register #(.width(1), .trigger("rising"), .Select("low")) register_4 (
    .D(multiplexer_4_out), .en(EN), .Q(out_20), .clk(CLK));  // open: clr
  Register #(.width(1), .trigger("rising"), .Select("low")) register_5 (
    .D(multiplexer_5_out), .en(EN), .Q(out_21), .clk(CLK));  // open: clr
  Register #(.width(32), .trigger("rising"), .Select("low")) register_6 (
    .D(multiplexer_6_out), .en(EN), .Q(R1_2), .clk(CLK));  // open: clr
  Register #(.width(32), .trigger("rising"), .Select("low")) register_7 (
    .D(multiplexer_7_out), .en(EN), .Q(R2_2), .clk(CLK));  // open: clr
  Register #(.width(32), .trigger("rising"), .Select("low")) register_8 (
    .D(multiplexer_8_out), .en(EN), .Q(ALU_Result_2), .clk(CLK));  // open: clr
  Register #(.width(32), .trigger("rising"), .Select("low")) register_9 (
    .D(multiplexer_9_out), .en(EN), .Q(WD_2), .clk(CLK));  // open: clr
  Register #(.width(32), .trigger("rising"), .Select("low")) register_10 (
    .D(multiplexer_10_out), .en(EN), .Q(PC_2), .clk(CLK));  // open: clr
  Register #(.width(5), .trigger("rising"), .Select("low")) register_11 (
    .D(multiplexer_11_out), .en(EN), .Q(Rt_2), .clk(CLK));  // open: clr
  Register #(.width(5), .trigger("rising"), .Select("low")) register_12 (
    .D(multiplexer_12_out), .en(EN), .Q(Rd_2), .clk(CLK));  // open: clr
  Register #(.width(32), .trigger("rising"), .Select("low")) register_13 (
    .D(multiplexer_13_out), .Q(IR_2), .clk(CLK));  // open: en, clr
endmodule

module DisplayTest (
  input  [15:0] in_1,
  input  [6:0] in_2,
  input  [6:0] in_3
);

  wire clock_1_out, clock_2_out;
  wire [6:0] keyboard_1_data;
  wire [31:0] undriven, undriven_2, undriven_3, undriven_4, undriven_5;

  Clock #(.highDuration(1), .lowDuration(1)) clock_1 (.out(clock_1_out));
  // LCD_Video lcd_video_1: pin names not known; wires that end beside it: clock_1_out, 1'b1, in_2, in_3, in_1, 1'b1
  Joystick #(.bits(4)) joystick_1 ();  // open: x, y
  Clock #(.highDuration(1), .lowDuration(1)) clock_2 (.out(clock_2_out));
  Keyboard #(.Char_bit_width(7), .buflen(32), .trigger("rising")) keyboard_1 (
    .clk(clock_2_out), .data(keyboard_1_data));  // open: re, clr, avail
  TTY #(.Char_bit_width(7), .rows(8), .cols(32), .trigger("rising")) tty_1 (
    .data(keyboard_1_data), .clk(clock_2_out));  // open: we, clr
  DotMatrix #(.inputtype("column"), .matrixcols(32), .matrixrows(32), .persist(0), .dotshape("square")) dotmatrix_1 (
    .col0(32'h1111), .col1(undriven), .col2(undriven_2), .col3(undriven_3), .col4(undriven_4),
    .col5(undriven_5));  // open: col6, col7, col8, col9, col10, col11, col12, col13, col14, col15, col16, col17, col18, col19, col20, col21, col22, col23, col24, col25, col26, col27, col28, col29, col30, col31
  LED #(.active("true")) led_1 ();  // open: in
  DotMatrix #(.inputtype("column"), .matrixcols(3), .matrixrows(3), .persist(0), .dotshape("square")) dotmatrix_2 (
    .col0(3'b001), .col1(3'b010), .col2(3'b100));
endmodule

module \数据相关检测  (
  input  R1_Used,
  input  [4:0] R1_num,
  input  [4:0] R2_num,
  input  R2_Used,
  input  [4:0] EX_WriteReg_num,
  input  [4:0] MEM_WriteReg_num,
  input  EX_RegWrite,
  input  MEM_RegWrite,
  output [1:0] ALU_Src1,
  output [1:0] R2EXMEM
);

  wire comparator_1_gt, comparator_2_gt, comparator_3_eq, comparator_4_eq, comparator_5_eq, comparator_6_eq;
  wire [4:0] controlled_buffer_1_out, controlled_buffer_2_out;

  assign controlled_buffer_1_out = comparator_1_gt ? R1_num : 5'bz;  // Controlled_Buffer controlled_buffer_1
  Comparator #(.width(5), .mode("unsigned")) comparator_1 (
    .a(R1_num), .b({5{1'b0}}), .gt(comparator_1_gt));  // open: eq, lt
  assign controlled_buffer_2_out = comparator_2_gt ? R2_num : 5'bz;  // Controlled_Buffer controlled_buffer_2
  Comparator #(.width(5), .mode("unsigned")) comparator_2 (
    .a(R2_num), .b({5{1'b0}}), .gt(comparator_2_gt));  // open: eq, lt
  // Probe on controlled_buffer_1_out
  Comparator #(.width(5), .mode("twosComplement")) comparator_3 (
    .a(controlled_buffer_1_out), .b(EX_WriteReg_num), .eq(comparator_3_eq));  // open: gt, lt
  Comparator #(.width(5), .mode("twosComplement")) comparator_4 (
    .a(controlled_buffer_2_out), .b(EX_WriteReg_num), .eq(comparator_4_eq));  // open: gt, lt
  Pull_Resistor #(.pull(0)) pull_resistor_1 (.node(comparator_3_eq));
  Comparator #(.width(5), .mode("twosComplement")) comparator_5 (
    .a(controlled_buffer_1_out), .b(MEM_WriteReg_num), .eq(comparator_5_eq));  // open: gt, lt
  Comparator #(.width(5), .mode("twosComplement")) comparator_6 (
    .a(controlled_buffer_2_out), .b(MEM_WriteReg_num), .eq(comparator_6_eq));  // open: gt, lt
  Pull_Resistor #(.pull(0)) pull_resistor_2 (.node(comparator_5_eq));
  Pull_Resistor #(.pull(0)) pull_resistor_3 (.node(comparator_4_eq));
  Pull_Resistor #(.pull(0)) pull_resistor_4 (.node(comparator_6_eq));
  and EXR1 (ALU_Src1[0], R1_Used, EX_RegWrite, comparator_3_eq);
  and EXR2 (R2EXMEM[0], R2_Used, comparator_4_eq, EX_RegWrite);
  and MEMR1 (ALU_Src1[1], R1_Used, comparator_5_eq, MEM_RegWrite);
  and MEMR2 (R2EXMEM[1], comparator_6_eq, MEM_RegWrite, R2_Used);

  // Notes on the sheet:
  //   注意出现11的情况为ID段读出的寄存器与EX，MEM段都相关，此时只需要将EX段的数据重定向即可
  //   注意出现11的情况为ID段读出的寄存器与EX，MEM段都相关，此时只需要将EX段的数据重定向即可
endmodule

module \源寄存器使用情况  (
  input  OP1,
  input  OP2,
  input  OP3,
  input  OP4,
  input  OP5,
  input  OP6,
  input  Funct1,
  input  Funct2,
  input  Funct3,
  input  Funct4,
  input  Funct5,
  input  Funct6,
  output R1_Used,
  output R2_Used,
  output LW
);

  wire and_1_out, and_2_out, and_3_out, and_4_out, and_5_out, and_6_out, and_7_out, and_8_out, and_9_out,
       and_10_out, and_11_out, and_12_out, and_13_out, and_14_out, and_15_out, and_16_out, and_17_out,
       and_18_out, and_19_out, and_20_out, and_21_out, and_22_out, and_23_out, and_24_out, and_25_out,
       and_26_out, and_27_out, and_28_out, and_29_out, and_30_out, and_31_out, and_32_out, and_33_out,
       and_34_out, and_35_out, and_36_out, and_37_out, and_38_out, and_39_out, and_40_out, and_41_out,
       and_42_out, and_43_out, and_44_out, and_45_out, not_1_out, not_2_out, not_3_out, not_4_out, not_5_out,
       not_6_out, not_7_out, not_8_out, not_9_out, not_10_out, not_11_out, not_12_out, not_13_out,
       not_14_out, not_15_out, not_16_out, not_17_out, not_18_out, not_19_out, not_20_out, not_21_out,
       not_22_out, not_23_out, not_24_out, not_25_out, not_26_out, not_27_out, not_28_out, not_29_out,
       not_30_out, not_31_out, not_32_out, not_33_out, not_34_out, not_35_out, not_36_out, not_37_out,
       not_38_out, not_39_out, not_40_out, not_41_out, not_42_out, not_43_out, not_44_out, not_45_out,
       not_46_out, not_47_out, not_48_out, not_49_out, not_50_out, not_51_out, not_52_out, not_53_out,
       not_54_out, not_55_out, not_56_out, not_57_out, not_58_out, not_59_out, not_60_out, not_61_out,
       not_62_out, not_63_out, not_64_out, not_65_out, not_66_out, not_67_out, not_68_out, not_69_out,
       not_70_out, not_71_out, not_72_out, not_73_out, not_74_out, not_75_out, not_76_out, not_77_out,
       not_78_out, not_79_out, not_80_out, not_81_out, not_82_out, not_83_out, not_84_out, not_85_out,
       not_86_out, not_87_out, not_88_out, not_89_out, not_90_out, not_91_out, not_92_out, not_93_out,
       not_94_out, not_95_out, not_96_out, not_97_out, not_98_out, not_99_out, not_100_out, not_101_out,
       not_102_out, not_103_out, not_104_out, not_105_out, not_106_out, not_107_out, not_108_out,
       not_109_out, not_110_out, not_111_out, not_112_out, not_113_out, not_114_out, not_115_out,
       not_116_out, not_117_out, not_118_out, not_119_out, not_120_out, not_121_out, not_122_out,
       not_123_out, not_124_out, not_125_out, not_126_out, not_127_out, not_128_out, not_129_out,
       not_130_out, not_131_out, not_132_out, not_133_out, not_134_out, not_135_out, not_136_out,
       not_137_out, not_138_out, not_139_out, not_140_out, not_141_out, not_142_out, not_143_out,
       not_144_out, not_145_out, not_146_out, not_147_out, not_148_out, not_149_out, not_150_out,
       not_151_out, not_152_out, not_153_out, not_154_out, not_155_out, not_156_out, not_157_out,
       not_158_out, not_159_out, not_160_out, not_161_out, not_162_out, not_163_out, not_164_out,
       not_165_out, not_166_out, not_167_out, not_168_out, not_169_out, not_170_out, not_171_out,
       not_172_out, not_173_out, not_174_out, not_175_out, not_176_out, not_177_out, not_178_out,
       not_179_out, not_180_out, not_181_out, not_182_out, not_183_out, not_184_out, not_185_out,
       not_186_out, not_187_out, not_188_out, not_189_out, not_190_out, not_191_out, not_192_out,
       not_193_out, not_194_out, not_195_out, not_196_out, not_197_out, not_198_out, not_199_out,
       not_200_out, not_201_out, not_202_out, not_203_out, not_204_out, not_205_out, not_206_out,
       not_207_out, not_208_out, not_209_out, not_210_out, not_211_out, not_212_out, not_213_out,
       not_214_out, not_215_out, not_216_out, not_217_out, not_218_out, not_219_out, not_220_out,
       not_221_out, not_222_out, not_223_out, not_224_out, not_225_out, not_226_out, not_227_out,
       not_228_out, not_229_out, not_230_out, not_231_out, not_232_out, not_233_out, not_234_out,
       not_235_out, not_236_out, not_237_out, not_238_out, not_239_out, not_240_out, not_241_out,
       not_242_out, not_243_out, not_244_out, not_245_out, not_246_out, not_247_out, not_248_out,
       not_249_out, not_250_out, not_251_out, not_252_out, not_253_out, not_254_out, not_255_out,
       not_256_out, not_257_out, not_258_out, not_259_out, not_260_out, not_261_out, not_262_out,
       not_263_out, not_264_out, not_265_out, not_266_out, not_267_out, not_268_out, not_269_out,
       not_270_out, not_271_out, not_272_out, not_273_out, not_274_out, not_275_out, not_276_out,
       not_277_out, not_278_out, not_279_out, not_280_out, not_281_out, not_282_out, not_283_out,
       not_284_out, not_285_out, not_286_out, not_287_out, not_288_out, not_289_out, not_290_out,
       not_291_out, not_292_out, not_293_out, not_294_out, not_295_out, not_296_out, not_297_out,
       not_298_out, not_299_out, not_300_out, not_301_out, not_302_out, not_303_out, not_304_out,
       not_305_out, not_306_out, not_307_out, not_308_out, not_309_out, not_310_out, not_311_out,
       not_312_out, not_313_out, not_314_out, not_315_out, not_316_out, not_317_out, not_318_out,
       not_319_out, not_320_out, not_321_out, not_322_out, not_323_out, not_324_out, not_325_out,
       not_326_out, not_327_out, not_328_out, not_329_out, not_330_out, not_331_out, not_332_out,
       not_333_out, not_334_out, not_335_out, not_336_out, not_337_out, not_338_out, not_339_out,
       not_340_out, not_341_out, not_342_out, not_343_out, not_344_out, not_345_out, not_346_out,
       not_347_out, not_348_out, not_349_out, not_350_out, not_351_out, not_352_out, not_353_out,
       not_354_out, not_355_out, not_356_out;

  not not_1 (not_1_out, OP6);
  not not_2 (not_2_out, OP5);
  not not_3 (not_3_out, OP4);
  not not_4 (not_4_out, OP3);
  not not_5 (not_5_out, OP2);
  not not_6 (not_6_out, OP1);
  not not_7 (not_7_out, Funct5);
  not not_8 (not_8_out, Funct4);
  not not_9 (not_9_out, Funct3);
  not not_10 (not_10_out, Funct2);
  not not_11 (not_11_out, Funct1);
  not not_12 (not_12_out, OP6);
  not not_13 (not_13_out, OP5);
  not not_14 (not_14_out, OP4);
  not not_15 (not_15_out, OP3);
  not not_16 (not_16_out, OP2);
  not not_17 (not_17_out, OP1);
  not not_18 (not_18_out, Funct5);
  not not_19 (not_19_out, Funct4);
  not not_20 (not_20_out, Funct3);
  not not_21 (not_21_out, Funct2);
  not not_22 (not_22_out, OP6);
  not not_23 (not_23_out, OP5);
  not not_24 (not_24_out, OP4);
  not not_25 (not_25_out, OP3);
  not not_26 (not_26_out, OP2);
  not not_27 (not_27_out, OP1);
  not not_28 (not_28_out, Funct5);
  not not_29 (not_29_out, Funct4);
  not not_30 (not_30_out, Funct3);
  not not_31 (not_31_out, Funct1);
  not not_32 (not_32_out, OP6);
  not not_33 (not_33_out, OP5);
  not not_34 (not_34_out, OP4);
  not not_35 (not_35_out, OP3);
  not not_36 (not_36_out, OP2);
  not not_37 (not_37_out, OP1);
  not not_38 (not_38_out, Funct5);
  not not_39 (not_39_out, Funct4);
  not not_40 (not_40_out, Funct2);
  not not_41 (not_41_out, Funct1);
  not not_42 (not_42_out, OP6);
  not not_43 (not_43_out, OP5);
  not not_44 (not_44_out, OP4);
  not not_45 (not_45_out, OP3);
  not not_46 (not_46_out, OP2);
  not not_47 (not_47_out, OP1);
  not not_48 (not_48_out, Funct5);
  not not_49 (not_49_out, Funct4);
  not not_50 (not_50_out, Funct2);
  not not_51 (not_51_out, OP6);
  not not_52 (not_52_out, OP5);
  not not_53 (not_53_out, OP4);
  not not_54 (not_54_out, OP3);
  not not_55 (not_55_out, OP2);
  not not_56 (not_56_out, OP1);
  not not_57 (not_57_out, Funct5);
  not not_58 (not_58_out, Funct4);
  not not_59 (not_59_out, OP6);
  not not_60 (not_60_out, OP5);
  not not_61 (not_61_out, OP4);
  not not_62 (not_62_out, OP3);
  not not_63 (not_63_out, OP2);
  not not_64 (not_64_out, OP1);
  not not_65 (not_65_out, Funct5);
  not not_66 (not_66_out, Funct3);
  not not_67 (not_67_out, Funct1);
  not not_68 (not_68_out, OP6);
  not not_69 (not_69_out, OP5);
  not not_70 (not_70_out, OP4);
  not not_71 (not_71_out, OP3);
  not not_72 (not_72_out, OP2);
  not not_73 (not_73_out, OP1);
  not not_74 (not_74_out, Funct5);
  not not_75 (not_75_out, Funct3);
  not not_76 (not_76_out, OP6);
  not not_77 (not_77_out, OP5);
  not not_78 (not_78_out, OP4);
  not not_79 (not_79_out, OP3);
  not not_80 (not_80_out, OP2);
  not not_81 (not_81_out, OP1);
  not not_82 (not_82_out, Funct6);
  not not_83 (not_83_out, Funct5);
  not not_84 (not_84_out, Funct3);
  not not_85 (not_85_out, Funct2);
  not not_86 (not_86_out, Funct1);
  not not_87 (not_87_out, OP6);
  not not_88 (not_88_out, OP5);
  not not_89 (not_89_out, OP4);
  not not_90 (not_90_out, OP3);
  not not_91 (not_91_out, OP2);
  not not_92 (not_92_out, OP1);
  not not_93 (not_93_out, Funct6);
  not not_94 (not_94_out, Funct5);
  not not_95 (not_95_out, Funct2);
  not not_96 (not_96_out, Funct1);
  not not_97 (not_97_out, OP6);
  not not_98 (not_98_out, OP5);
  not not_99 (not_99_out, OP4);
  not not_100 (not_100_out, OP2);
  not not_101 (not_101_out, OP1);
  not not_102 (not_102_out, OP6);
  not not_103 (not_103_out, OP5);
  not not_104 (not_104_out, OP4);
  not not_105 (not_105_out, OP2);
  not not_106 (not_106_out, OP6);
  not not_107 (not_107_out, OP5);
  not not_108 (not_108_out, OP3);
  not not_109 (not_109_out, OP2);
  not not_110 (not_110_out, OP1);
  not not_111 (not_111_out, OP6);
  not not_112 (not_112_out, OP5);
  not not_113 (not_113_out, OP2);
  not not_114 (not_114_out, OP1);
  not not_115 (not_115_out, OP6);
  not not_116 (not_116_out, OP5);
  not not_117 (not_117_out, OP3);
  not not_118 (not_118_out, OP2);
  not not_119 (not_119_out, OP6);
  not not_120 (not_120_out, OP5);
  not not_121 (not_121_out, OP3);
  not not_122 (not_122_out, OP1);
  not not_123 (not_123_out, OP6);
  not not_124 (not_124_out, OP5);
  not not_125 (not_125_out, OP2);
  not not_126 (not_126_out, OP5);
  not not_127 (not_127_out, OP4);
  not not_128 (not_128_out, OP3);
  not not_129 (not_129_out, OP5);
  not not_130 (not_130_out, OP3);
  not not_131 (not_131_out, OP6);
  not not_132 (not_132_out, OP5);
  not not_133 (not_133_out, OP4);
  not not_134 (not_134_out, OP3);
  not not_135 (not_135_out, OP2);
  not not_136 (not_136_out, OP1);
  not not_137 (not_137_out, Funct5);
  not not_138 (not_138_out, Funct4);
  not not_139 (not_139_out, Funct3);
  not not_140 (not_140_out, OP6);
  not not_141 (not_141_out, OP5);
  not not_142 (not_142_out, OP4);
  not not_143 (not_143_out, OP3);
  not not_144 (not_144_out, OP2);
  not not_145 (not_145_out, OP1);
  not not_146 (not_146_out, Funct5);
  not not_147 (not_147_out, Funct4);
  not not_148 (not_148_out, Funct1);
  not not_149 (not_149_out, OP6);
  not not_150 (not_150_out, OP5);
  not not_151 (not_151_out, OP4);
  not not_152 (not_152_out, OP3);
  not not_153 (not_153_out, OP2);
  not not_154 (not_154_out, OP1);
  not not_155 (not_155_out, Funct6);
  not not_156 (not_156_out, Funct5);
  not not_157 (not_157_out, Funct4);
  not not_158 (not_158_out, Funct2);
  not not_159 (not_159_out, Funct1);
  not not_160 (not_160_out, OP6);
  not not_161 (not_161_out, OP5);
  not not_162 (not_162_out, OP4);
  not not_163 (not_163_out, OP3);
  not not_164 (not_164_out, OP2);
  not not_165 (not_165_out, OP1);
  not not_166 (not_166_out, Funct6);
  not not_167 (not_167_out, Funct5);
  not not_168 (not_168_out, Funct4);
  not not_169 (not_169_out, Funct1);
  not not_170 (not_170_out, OP6);
  not not_171 (not_171_out, OP5);
  not not_172 (not_172_out, OP4);
  not not_173 (not_173_out, OP3);
  not not_174 (not_174_out, OP2);
  not not_175 (not_175_out, OP1);
  not not_176 (not_176_out, Funct6);
  not not_177 (not_177_out, Funct5);
  not not_178 (not_178_out, Funct4);
  not not_179 (not_179_out, OP6);
  not not_180 (not_180_out, OP5);
  not not_181 (not_181_out, OP1);
  not not_182 (not_182_out, OP6);
  not not_183 (not_183_out, OP5);
  not not_184 (not_184_out, OP3);
  not not_185 (not_185_out, OP6);
  not not_186 (not_186_out, OP5);
  not not_187 (not_187_out, OP4);
  not not_188 (not_188_out, OP3);
  not not_189 (not_189_out, OP2);
  not not_190 (not_190_out, OP1);
  not not_191 (not_191_out, Funct6);
  not not_192 (not_192_out, Funct5);
  not not_193 (not_193_out, Funct4);
  not not_194 (not_194_out, Funct3);
  not not_195 (not_195_out, Funct2);
  not not_196 (not_196_out, Funct1);
  not not_197 (not_197_out, OP6);
  not not_198 (not_198_out, OP5);
  not not_199 (not_199_out, OP4);
  not not_200 (not_200_out, OP3);
  not not_201 (not_201_out, OP2);
  not not_202 (not_202_out, OP1);
  not not_203 (not_203_out, Funct6);
  not not_204 (not_204_out, Funct5);
  not not_205 (not_205_out, Funct4);
  not not_206 (not_206_out, Funct3);
  not not_207 (not_207_out, OP6);
  not not_208 (not_208_out, OP5);
  not not_209 (not_209_out, OP4);
  not not_210 (not_210_out, OP3);
  not not_211 (not_211_out, OP2);
  not not_212 (not_212_out, OP1);
  not not_213 (not_213_out, Funct6);
  not not_214 (not_214_out, Funct5);
  not not_215 (not_215_out, Funct4);
  not not_216 (not_216_out, Funct3);
  not not_217 (not_217_out, Funct1);
  not not_218 (not_218_out, OP6);
  not not_219 (not_219_out, OP5);
  not not_220 (not_220_out, OP4);
  not not_221 (not_221_out, OP3);
  not not_222 (not_222_out, OP2);
  not not_223 (not_223_out, OP1);
  not not_224 (not_224_out, Funct5);
  not not_225 (not_225_out, Funct4);
  not not_226 (not_226_out, Funct3);
  not not_227 (not_227_out, Funct2);
  not not_228 (not_228_out, Funct1);
  not not_229 (not_229_out, OP6);
  not not_230 (not_230_out, OP5);
  not not_231 (not_231_out, OP4);
  not not_232 (not_232_out, OP3);
  not not_233 (not_233_out, OP2);
  not not_234 (not_234_out, OP1);
  not not_235 (not_235_out, Funct5);
  not not_236 (not_236_out, Funct4);
  not not_237 (not_237_out, Funct3);
  not not_238 (not_238_out, Funct2);
  not not_239 (not_239_out, OP6);
  not not_240 (not_240_out, OP5);
  not not_241 (not_241_out, OP4);
  not not_242 (not_242_out, OP3);
  not not_243 (not_243_out, OP2);
  not not_244 (not_244_out, OP1);
  not not_245 (not_245_out, Funct5);
  not not_246 (not_246_out, Funct4);
  not not_247 (not_247_out, Funct3);
  not not_248 (not_248_out, Funct1);
  not not_249 (not_249_out, OP6);
  not not_250 (not_250_out, OP5);
  not not_251 (not_251_out, OP4);
  not not_252 (not_252_out, OP3);
  not not_253 (not_253_out, OP2);
  not not_254 (not_254_out, OP1);
  not not_255 (not_255_out, Funct5);
  not not_256 (not_256_out, Funct4);
  not not_257 (not_257_out, Funct2);
  not not_258 (not_258_out, Funct1);
  not not_259 (not_259_out, OP6);
  not not_260 (not_260_out, OP5);
  not not_261 (not_261_out, OP4);
  not not_262 (not_262_out, OP3);
  not not_263 (not_263_out, OP2);
  not not_264 (not_264_out, OP1);
  not not_265 (not_265_out, Funct5);
  not not_266 (not_266_out, Funct4);
  not not_267 (not_267_out, Funct2);
  not not_268 (not_268_out, OP6);
  not not_269 (not_269_out, OP5);
  not not_270 (not_270_out, OP4);
  not not_271 (not_271_out, OP3);
  not not_272 (not_272_out, OP2);
  not not_273 (not_273_out, OP1);
  not not_274 (not_274_out, Funct5);
  not not_275 (not_275_out, Funct4);
  not not_276 (not_276_out, OP6);
  not not_277 (not_277_out, OP5);
  not not_278 (not_278_out, OP4);
  not not_279 (not_279_out, OP3);
  not not_280 (not_280_out, OP2);
  not not_281 (not_281_out, OP1);
  not not_282 (not_282_out, Funct5);
  not not_283 (not_283_out, Funct3);
  not not_284 (not_284_out, Funct1);
  not not_285 (not_285_out, OP6);
  not not_286 (not_286_out, OP5);
  not not_287 (not_287_out, OP4);
  not not_288 (not_288_out, OP3);
  not not_289 (not_289_out, OP2);
  not not_290 (not_290_out, OP1);
  not not_291 (not_291_out, Funct6);
  not not_292 (not_292_out, Funct5);
  not not_293 (not_293_out, Funct2);
  not not_294 (not_294_out, Funct1);
  not not_295 (not_295_out, OP6);
  not not_296 (not_296_out, OP5);
  not not_297 (not_297_out, OP4);
  not not_298 (not_298_out, OP2);
  not not_299 (not_299_out, OP1);
  not not_300 (not_300_out, OP6);
  not not_301 (not_301_out, OP5);
  not not_302 (not_302_out, OP4);
  not not_303 (not_303_out, OP2);
  not not_304 (not_304_out, OP5);
  not not_305 (not_305_out, OP3);
  not not_306 (not_306_out, OP6);
  not not_307 (not_307_out, OP5);
  not not_308 (not_308_out, OP4);
  not not_309 (not_309_out, OP3);
  not not_310 (not_310_out, OP2);
  not not_311 (not_311_out, OP1);
  not not_312 (not_312_out, Funct5);
  not not_313 (not_313_out, Funct4);
  not not_314 (not_314_out, Funct3);
  not not_315 (not_315_out, OP6);
  not not_316 (not_316_out, OP5);
  not not_317 (not_317_out, OP4);
  not not_318 (not_318_out, OP3);
  not not_319 (not_319_out, OP2);
  not not_320 (not_320_out, OP1);
  not not_321 (not_321_out, Funct5);
  not not_322 (not_322_out, Funct4);
  not not_323 (not_323_out, Funct1);
  not not_324 (not_324_out, OP6);
  not not_325 (not_325_out, OP5);
  not not_326 (not_326_out, OP4);
  not not_327 (not_327_out, OP3);
  not not_328 (not_328_out, OP2);
  not not_329 (not_329_out, OP1);
  not not_330 (not_330_out, Funct6);
  not not_331 (not_331_out, Funct5);
  not not_332 (not_332_out, Funct4);
  not not_333 (not_333_out, Funct2);
  not not_334 (not_334_out, Funct1);
  not not_335 (not_335_out, OP6);
  not not_336 (not_336_out, OP5);
  not not_337 (not_337_out, OP4);
  not not_338 (not_338_out, OP3);
  not not_339 (not_339_out, OP2);
  not not_340 (not_340_out, OP1);
  not not_341 (not_341_out, Funct6);
  not not_342 (not_342_out, Funct5);
  not not_343 (not_343_out, Funct4);
  not not_344 (not_344_out, Funct1);
  not not_345 (not_345_out, OP6);
  not not_346 (not_346_out, OP5);
  not not_347 (not_347_out, OP4);
  not not_348 (not_348_out, OP3);
  not not_349 (not_349_out, OP2);
  not not_350 (not_350_out, OP1);
  not not_351 (not_351_out, Funct6);
  not not_352 (not_352_out, Funct5);
  not not_353 (not_353_out, Funct4);
  not not_354 (not_354_out, OP5);
  not not_355 (not_355_out, OP4);
  not not_356 (not_356_out, OP3);
  and and_1 (and_1_out, not_1_out, not_2_out, not_3_out, not_4_out, not_5_out, not_6_out, Funct6, not_7_out, not_8_out, not_9_out, not_10_out, not_11_out);
  and and_2 (and_2_out, not_12_out, not_13_out, not_14_out, not_15_out, not_16_out, not_17_out, Funct6, not_18_out, not_19_out, not_20_out, not_21_out, Funct1);
  and and_3 (and_3_out, not_22_out, not_23_out, not_24_out, not_25_out, not_26_out, not_27_out, Funct6, not_28_out, not_29_out, not_30_out, Funct2, not_31_out);
  and and_4 (and_4_out, not_32_out, not_33_out, not_34_out, not_35_out, not_36_out, not_37_out, Funct6, not_38_out, not_39_out, Funct3, not_40_out, not_41_out);
  and and_5 (and_5_out, not_42_out, not_43_out, not_44_out, not_45_out, not_46_out, not_47_out, Funct6, not_48_out, not_49_out, Funct3, not_50_out, Funct1);
  and and_6 (and_6_out, not_51_out, not_52_out, not_53_out, not_54_out, not_55_out, not_56_out, Funct6, not_57_out, not_58_out, Funct3, Funct2, Funct1);
  and and_7 (and_7_out, not_59_out, not_60_out, not_61_out, not_62_out, not_63_out, not_64_out, Funct6, not_65_out, Funct4, not_66_out, Funct2, not_67_out);
  and and_8 (and_8_out, not_68_out, not_69_out, not_70_out, not_71_out, not_72_out, not_73_out, Funct6, not_74_out, Funct4, not_75_out, Funct2, Funct1);
  and and_9 (and_9_out, not_76_out, not_77_out, not_78_out, not_79_out, not_80_out, not_81_out, not_82_out, not_83_out, Funct4, not_84_out, not_85_out, not_86_out);
  and and_10 (and_10_out, not_87_out, not_88_out, not_89_out, not_90_out, not_91_out, not_92_out, not_93_out, not_94_out, Funct4, Funct3, not_95_out, not_96_out);
  and and_11 (and_11_out, not_97_out, not_98_out, not_99_out, OP3, not_100_out, not_101_out);
  and and_12 (and_12_out, not_102_out, not_103_out, not_104_out, OP3, not_105_out, OP1);
  and and_13 (and_13_out, not_106_out, not_107_out, OP4, not_108_out, not_109_out, not_110_out);
  and and_14 (and_14_out, not_111_out, not_112_out, OP4, OP3, not_113_out, not_114_out);
  and and_15 (and_15_out, not_115_out, not_116_out, OP4, not_117_out, not_118_out, OP1);
  and and_16 (and_16_out, not_119_out, not_120_out, OP4, not_121_out, OP2, not_122_out);
  and and_17 (and_17_out, not_123_out, not_124_out, OP4, OP3, not_125_out, OP1);
  and and_18 (and_18_out, OP6, not_126_out, not_127_out, not_128_out, OP2, OP1);
  and and_19 (and_19_out, OP6, not_129_out, OP4, not_130_out, OP2, OP1);
  and and_20 (and_20_out, not_131_out, not_132_out, not_133_out, not_134_out, not_135_out, not_136_out, Funct6, not_137_out, not_138_out, not_139_out, Funct2, Funct1);
  and and_21 (and_21_out, not_140_out, not_141_out, not_142_out, not_143_out, not_144_out, not_145_out, Funct6, not_146_out, not_147_out, Funct3, Funct2, not_148_out);
  and and_22 (and_22_out, not_149_out, not_150_out, not_151_out, not_152_out, not_153_out, not_154_out, not_155_out, not_156_out, not_157_out, Funct3, not_158_out, not_159_out);
  and and_23 (and_23_out, not_160_out, not_161_out, not_162_out, not_163_out, not_164_out, not_165_out, not_166_out, not_167_out, not_168_out, Funct3, Funct2, not_169_out);
  and and_24 (and_24_out, not_170_out, not_171_out, not_172_out, not_173_out, not_174_out, not_175_out, not_176_out, not_177_out, not_178_out, Funct3, Funct2, Funct1);
  and and_25 (and_25_out, not_179_out, not_180_out, OP4, OP3, OP2, not_181_out);
  and and_26 (and_26_out, not_182_out, not_183_out, OP4, not_184_out, OP2, OP1);
  and and_27 (and_27_out, not_185_out, not_186_out, not_187_out, not_188_out, not_189_out, not_190_out, not_191_out, not_192_out, not_193_out, not_194_out, not_195_out, not_196_out);
  and and_28 (and_28_out, not_197_out, not_198_out, not_199_out, not_200_out, not_201_out, not_202_out, not_203_out, not_204_out, not_205_out, not_206_out, Funct2, Funct1);
  and and_29 (and_29_out, not_207_out, not_208_out, not_209_out, not_210_out, not_211_out, not_212_out, not_213_out, not_214_out, not_215_out, not_216_out, Funct2, not_217_out);
  and and_30 (and_30_out, not_218_out, not_219_out, not_220_out, not_221_out, not_222_out, not_223_out, Funct6, not_224_out, not_225_out, not_226_out, not_227_out, not_228_out);
  and and_31 (and_31_out, not_229_out, not_230_out, not_231_out, not_232_out, not_233_out, not_234_out, Funct6, not_235_out, not_236_out, not_237_out, not_238_out, Funct1);
  and and_32 (and_32_out, not_239_out, not_240_out, not_241_out, not_242_out, not_243_out, not_244_out, Funct6, not_245_out, not_246_out, not_247_out, Funct2, not_248_out);
  and and_33 (and_33_out, not_249_out, not_250_out, not_251_out, not_252_out, not_253_out, not_254_out, Funct6, not_255_out, not_256_out, Funct3, not_257_out, not_258_out);
  and and_34 (and_34_out, not_259_out, not_260_out, not_261_out, not_262_out, not_263_out, not_264_out, Funct6, not_265_out, not_266_out, Funct3, not_267_out, Funct1);
  and and_35 (and_35_out, not_268_out, not_269_out, not_270_out, not_271_out, not_272_out, not_273_out, Funct6, not_274_out, not_275_out, Funct3, Funct2, Funct1);
  and and_36 (and_36_out, not_276_out, not_277_out, not_278_out, not_279_out, not_280_out, not_281_out, Funct6, not_282_out, Funct4, not_283_out, Funct2, not_284_out);
  and and_37 (and_37_out, not_285_out, not_286_out, not_287_out, not_288_out, not_289_out, not_290_out, not_291_out, not_292_out, Funct4, Funct3, not_293_out, not_294_out);
  and and_38 (and_38_out, not_295_out, not_296_out, not_297_out, OP3, not_298_out, not_299_out);
  and and_39 (and_39_out, not_300_out, not_301_out, not_302_out, OP3, not_303_out, OP1);
  and and_40 (and_40_out, OP6, not_304_out, OP4, not_305_out, OP2, OP1);
  and and_41 (and_41_out, not_306_out, not_307_out, not_308_out, not_309_out, not_310_out, not_311_out, Funct6, not_312_out, not_313_out, not_314_out, Funct2, Funct1);
  and and_42 (and_42_out, not_315_out, not_316_out, not_317_out, not_318_out, not_319_out, not_320_out, Funct6, not_321_out, not_322_out, Funct3, Funct2, not_323_out);
  and and_43 (and_43_out, not_324_out, not_325_out, not_326_out, not_327_out, not_328_out, not_329_out, not_330_out, not_331_out, not_332_out, Funct3, not_333_out, not_334_out);
  and and_44 (and_44_out, not_335_out, not_336_out, not_337_out, not_338_out, not_339_out, not_340_out, not_341_out, not_342_out, not_343_out, Funct3, Funct2, not_344_out);
  and and_45 (and_45_out, not_345_out, not_346_out, not_347_out, not_348_out, not_349_out, not_350_out, not_351_out, not_352_out, not_353_out, Funct3, Funct2, Funct1);
  and and_46 (LW, OP6, not_354_out, not_355_out, not_356_out, OP2, OP1);
  or or_1 (R1_Used, and_1_out, and_2_out, and_3_out, and_4_out, and_5_out, and_6_out, and_7_out, and_8_out, and_9_out, and_10_out, and_11_out, and_12_out, and_13_out, and_14_out, and_15_out, and_16_out, and_17_out, and_18_out, and_19_out, and_20_out, and_21_out, and_22_out, and_23_out, and_24_out, and_25_out, and_26_out);
  or or_2 (R2_Used, and_27_out, and_28_out, and_29_out, and_30_out, and_31_out, and_32_out, and_33_out, and_34_out, and_35_out, and_36_out, and_37_out, and_38_out, and_39_out, and_40_out, and_41_out, and_42_out, and_43_out, and_44_out, and_45_out);
endmodule

module \load_use检测  (
  input  [4:0] EX_WriteReg_num,
  input  EX_LW,
  input  R1_Used,
  input  [4:0] R1_num,
  input  R2_Used,
  input  [4:0] R2_num,
  output load_use_Detected
);

  wire and_1_out, and_2_out, comparator_1_gt, comparator_2_gt, comparator_3_eq, comparator_4_eq;
  wire [4:0] controlled_buffer_1_out, controlled_buffer_2_out;

  Comparator #(.width(5), .mode("unsigned")) comparator_1 (
    .a(R1_num), .b({5{1'b0}}), .gt(comparator_1_gt));  // open: eq, lt
  Comparator #(.width(5), .mode("unsigned")) comparator_2 (
    .a(R2_num), .b({5{1'b0}}), .gt(comparator_2_gt));  // open: eq, lt
  assign controlled_buffer_1_out = comparator_1_gt ? R1_num : 5'bz;  // Controlled_Buffer controlled_buffer_1
  assign controlled_buffer_2_out = comparator_2_gt ? R2_num : 5'bz;  // Controlled_Buffer controlled_buffer_2
  // Probe on controlled_buffer_1_out
  Comparator #(.width(5), .mode("twosComplement")) comparator_3 (
    .a(EX_WriteReg_num), .b(controlled_buffer_1_out), .eq(comparator_3_eq));  // open: gt, lt
  Comparator #(.width(5), .mode("twosComplement")) comparator_4 (
    .a(EX_WriteReg_num), .b(controlled_buffer_2_out), .eq(comparator_4_eq));  // open: gt, lt
  Pull_Resistor #(.pull(0)) pull_resistor_1 (.node(comparator_3_eq));
  Pull_Resistor #(.pull(0)) pull_resistor_2 (.node(comparator_4_eq));
  and and_1 (and_1_out, EX_LW, R1_Used, comparator_3_eq);
  and and_2 (and_2_out, EX_LW, R2_Used, comparator_4_eq);
  or or_1 (load_use_Detected, and_1_out, and_2_out);

  // Notes on the sheet:
  //   R1与前一条指令产生load-use相关
  //   R2与前一条指令产生load-use相关
endmodule

module \单周期MIPS_31条指令  (
);

  wire alu_2_equal, ALUSRC, and_3_out, and_4_out, CLK, comparator_1_eq, comparator_2_eq, DisplayHex, Halt,
       JAL, MemToReg, MemWrite, not_1_out, or_1_out, RegDst, ShiftVar, signedExt, \硬布线控制器_1_beq ,
       \硬布线控制器_1_bne , \硬布线控制器_1_jmp , \硬布线控制器_1_jr , \硬布线控制器_1_regwrite , \硬布线控制器_1_syscall ;
  wire [1:0] W_num;
  wire [2:0] Branch;
  wire [3:0] \硬布线控制器_1_alu_op ;
  wire [4:0] multiplexer_2_out, multiplexer_3_out, multiplexer_4_out, multiplexer_7_out;
  wire [27:0] alu_1_result;
  wire [31:0] alu_2_result, alu_3_result, LedData, mips_ram_1_p5, multiplexer_1_out, multiplexer_5_out,
       multiplexer_6_out, multiplexer_8_out, PC_q, regifile_1_r1, rt, shifter_1_out, \符号扩展_1_out_3 ;
  wire [31:2] rom_1_data;
  wire [31:26] rom_1_data_2;

  Hex_Digit_Display hex_digit_display_1 (.value(LedData[31:28]));  // open: dp
  Hex_Digit_Display hex_digit_display_2 (.value(LedData[27:24]));  // open: dp
  Hex_Digit_Display hex_digit_display_3 (.value(LedData[23:20]));  // open: dp
  Hex_Digit_Display hex_digit_display_4 (.value(LedData[15:12]));  // open: dp
  Hex_Digit_Display hex_digit_display_5 (.value(LedData[19:16]));  // open: dp
  Clock #(.highDuration(1), .lowDuration(1)) clock_1 (.out(CLK));
  Multiplexer #(.select(3), .width(32), .disabled("Z"), .enable("false")) multiplexer_1 (
    .in0({rom_1_data[31:28], alu_1_result}), .in1(alu_3_result), .in2(regifile_1_r1),
    .in3({rom_1_data, 2'b00}), .in4({rom_1_data, 2'b00}), .out(multiplexer_1_out), .sel(Branch));  // open: in5, in6, in7
  Hex_Digit_Display hex_digit_display_6 (.value(LedData[7:4]));  // open: dp
  Hex_Digit_Display hex_digit_display_7 (.value(LedData[11:8]));  // open: dp
  Register #(.width(32), .trigger("rising"), .Select("low")) PC (
    .D(multiplexer_1_out), .en(not_1_out), .Q(PC_q), .clk(CLK));  // open: clr
  not not_1 (not_1_out, Halt);
  Hex_Digit_Display hex_digit_display_8 (.value(LedData[3:0]));  // open: dp
  Priority_Encoder #(.select(3), .disabled("Z")) priority_encoder_1 (
    .in0(1'b1), .in1(or_1_out), .in2(\硬布线控制器_1_jr ), .in3(\硬布线控制器_1_jmp ), .in4(JAL), .out(Branch));  // open: in5, in6, in7, gs, en_out, en_in
  Priority_Encoder #(.select(2), .disabled("Z")) priority_encoder_2 (
    .in0(1'b1), .in1(RegDst), .in2(JAL), .out(W_num));  // open: in3, gs, en_out, en_in
  ALU alu_1 (
    .X(PC_q), .Y(32'h4), .AluOP(4'b0101), .Result({rom_1_data[31:28], alu_1_result}));  // open: shamt, Equal, Result_2
  Register #(.width(32), .trigger("rising"), .Select("low")) register_1 (
    .D(rt), .Q(LedData), .clk(DisplayHex));  // open: en, clr
  ROM #(.addrWidth(10), .dataWidth(32), .Select("high")) rom_1 (
    .addr(PC_q[11:2]), .data({rom_1_data_2, rom_1_data[27:2]}));
  \硬布线控制器  \u_硬布线控制器_1  (
    .Func(rom_1_data[7:2]), .OP(rom_1_data_2), .ALU_OP(\硬布线控制器_1_alu_op ), .MemToReg(MemToReg),
    .MemWrite(MemWrite), .ALU_SRC(ALUSRC), .RegWrite(\硬布线控制器_1_regwrite ), .SysCALL(\硬布线控制器_1_syscall ),
    .SignedExt(signedExt), .RegDst(RegDst), .JR(\硬布线控制器_1_jr ), .JMP(\硬布线控制器_1_jmp ), .Beq(\硬布线控制器_1_beq ),
    .JAL(JAL), .Bne(\硬布线控制器_1_bne ), .ShiftVar(ShiftVar));
  Multiplexer #(.select(1), .width(5), .disabled("Z"), .enable("false")) multiplexer_2 (
    .in0(rom_1_data[27:23]), .in1(5'b00010), .out(multiplexer_2_out), .sel(\硬布线控制器_1_syscall ));
  Multiplexer #(.select(1), .width(5), .disabled("Z"), .enable("false")) multiplexer_3 (
    .in0(rom_1_data[22:18]), .in1(5'b00100), .out(multiplexer_3_out), .sel(\硬布线控制器_1_syscall ));
  // Probe on multiplexer_4_out
  Multiplexer #(.select(2), .width(5), .disabled("Z"), .enable("false")) multiplexer_4 (
    .in0(rom_1_data[22:18]), .in1(rom_1_data[17:13]), .in2({5{1'b1}}), .out(multiplexer_4_out), .sel(W_num));  // open: in3
  \符号扩展  \u_符号扩展_1  (.in_1(rom_1_data[17:2]), .out_3(\符号扩展_1_out_3 ), .in_2(signedExt));
  Multiplexer #(.select(1), .width(32), .disabled("Z"), .enable("false")) multiplexer_5 (
    .in0(multiplexer_8_out), .in1({rom_1_data[31:28], alu_1_result}), .out(multiplexer_5_out), .sel(JAL));
  Regifile regifile_1 (
    .Din(multiplexer_5_out), .Clk(CLK), .R1(regifile_1_r1), .R2(rt), .WE(\硬布线控制器_1_regwrite ),
    .W_num(multiplexer_4_out), .R1_num(multiplexer_2_out), .R2_num(multiplexer_3_out));
  Comparator #(.width(32), .mode("twosComplement")) comparator_1 (
    .a(32'h22), .b(regifile_1_r1), .eq(comparator_1_eq));  // open: gt, lt
  and and_1 (DisplayHex, comparator_1_eq, \硬布线控制器_1_syscall );
  Comparator #(.width(32), .mode("twosComplement")) comparator_2 (
    .a(32'ha), .b(regifile_1_r1), .eq(comparator_2_eq));  // open: gt, lt
  and and_2 (Halt, comparator_2_eq, \硬布线控制器_1_syscall );
  Multiplexer #(.select(1), .width(32), .disabled("Z"), .enable("false")) multiplexer_6 (
    .in0(rt), .in1(\符号扩展_1_out_3 ), .out(multiplexer_6_out), .sel(ALUSRC));
  Multiplexer #(.select(1), .width(5), .disabled("Z"), .enable("false")) multiplexer_7 (
    .in0(rom_1_data[12:8]), .in1(regifile_1_r1[4:0]), .out(multiplexer_7_out), .sel(ShiftVar));
  Shifter #(.width(32), .shift("ll")) shifter_1 (.in(\符号扩展_1_out_3 ), .\dist (5'b00010), .out(shifter_1_out));
  and and_3 (and_3_out, \硬布线控制器_1_beq , alu_2_equal);
  and and_4 (and_4_out, \硬布线控制器_1_bne , ~alu_2_equal);  // AND_Gate
  ALU alu_2 (
    .shamt(multiplexer_7_out), .X(regifile_1_r1), .Y(multiplexer_6_out), .AluOP(\硬布线控制器_1_alu_op ),
    .Equal(alu_2_equal), .Result(alu_2_result));  // open: Result_2
  ALU alu_3 (
    .X(shifter_1_out), .Y({rom_1_data[31:28], alu_1_result}), .AluOP(4'b0101), .Result(alu_3_result));  // open: shamt, Equal, Result_2
  or or_1 (or_1_out, and_3_out, and_4_out);
  // MIPS_RAM mips_ram_1: pin names not known; wires that end beside it: alu_2_result[25:2], rt, MemWrite, CLK, mips_ram_1_p5
  Multiplexer #(.select(1), .width(32), .disabled("Z"), .enable("false")) multiplexer_8 (
    .in0(alu_2_result), .in1(mips_ram_1_p5), .out(multiplexer_8_out), .sel(MemToReg));

  // Notes on the sheet:
  //   数码管输出
  //   PC+4
  //   J型指令的跳转地址
  //   I型指令的跳转地址
  //   跳转信号生成
  //   rs
  //   rt
  //   contents of rom_1 (hex, n*v repeats v):
  //   20110001 8000c05 20110001 20120002 20130003 8000c09 20110001 20120002 20130003 8000c0d 20110001
  //   20120002 20130003 8000c11 20110001 20120002 20130003 c000cb8 20100001 20110001 118fc0 112020
  //   20020022 c 118882 12200001 8000c15 112020 20020022 c 20110001 118880 112020 20020022 c 12200001
  //   8000c1f 20110001 118fc0 112020 20020022 c 1188c3 112020 20020022 c 118903 112020 20020022 c 118903
  //   112020 20020022 c 118903 112020 20020022 c 118903 112020 20020022 c 118903 112020 20020022 c 118903
  //   112020 20020022 c 118903 112020 20020022 c 20100001 109fc0 139fc3 8021 2012000c 24160003 26100001
  //   3210000f 20080008 20090001 139900 2709825 132020 20020022 c 1094022 1500fff9 22100001 2018000f
  //   2188024 108700 20080008 20090001 139902 2709825 132021 20020022 c 1094022 1500fff9 108702 2c9b022
  //   12c00001 8000c50 4020 1084027 84400 3508ffff 82021 20020022 c 2010ffff 20110000 ae300000 22100001
  //   22310004 ae300000 22100001 22310004 ae300000 22100001 22310004 ae300000 22100001 22310004 ae300000
  //   22100001 22310004 ae300000 22100001 22310004 ae300000 22100001 22310004 ae300000 22100001 22310004
  //   ae300000 22100001 22310004 ae300000 22100001 22310004 ae300000 22100001 22310004 ae300000 22100001
  //   22310004 ae300000 22100001 22310004 ae300000 22100001 22310004 ae300000 22100001 22310004 ae300000
  //   22100001 22310004 22100001 8020 2011003c 8e130000 8e340000 274402a 11000002 ae330000 ae140000
  //   2231fffc 1611fff8 102020 20020022 c 22100004 2011003c 1611fff2 2002000a c 20100000 22100001 102020
  //   20020022 c 22100002 102020 20020022 c 22100003 102020 20020022 c 22100004 102020 20020022 c 22100005
  //   102020 20020022 c 22100006 102020 20020022 c 22100007 102020 20020022 c 22100008 102020 20020022
  //   20020022 c 3e00008
  //   rd
  //   shamt
  //   Imm
  //   Jump
  //   JR
  //   OP
  //   Func
  //   Beq
  //   Bne
  //   JAL
  //   syscall
  //   RegWrite
  //   PC+4
  //   ALUOP
  //   数据存储器
endmodule
